// Logisim project CMOS_Logic.circ as structural Verilog: 11 circuits, main circuit Exercise_184A
module Exercise_184A (
  input  A,
  input  B,
  input  C,
  input  D,
  output Y
);

  wire transistor_6_out, transistor_7_out, transistor_8_out;

  Transistor transistor_1 (.in(1'b1), .out(Y), .gate(D));
  Transistor transistor_2 (.in(1'b1), .out(Y), .gate(C));
  Transistor transistor_3 (.in(1'b1), .out(Y), .gate(B));
  Transistor transistor_4 (.in(1'b1), .out(Y), .gate(A));
  Transistor #(.\type ("n")) transistor_5 (.in(transistor_6_out), .out(Y), .gate(A));
  Transistor #(.\type ("n")) transistor_6 (.in(transistor_7_out), .out(transistor_6_out), .gate(B));
  Transistor #(.\type ("n")) transistor_7 (.in(transistor_8_out), .out(transistor_7_out), .gate(C));
  Transistor #(.\type ("n")) transistor_8 (.in(1'b0), .out(transistor_8_out), .gate(D));
endmodule

module Exercise_184B (
  input  A,
  input  B,
  input  C,
  output Y
);

  wire transistor_1_out, transistor_2_out, transistor_6_out, transistor_10_out;

  Transistor transistor_1 (.in(1'b1), .out(transistor_1_out), .gate(A));
  Transistor transistor_2 (.in(transistor_1_out), .out(transistor_2_out), .gate(B));
  Transistor #(.\type ("n")) transistor_3 (.in(1'b0), .out(transistor_2_out), .gate(B));
  Transistor #(.\type ("n")) transistor_4 (.in(1'b0), .out(transistor_2_out), .gate(A));
  Transistor transistor_5 (.in(1'b1), .out(Y), .gate(transistor_6_out));
  Transistor transistor_6 (.in(1'b1), .out(transistor_6_out), .gate(transistor_2_out));
  Transistor #(.\type ("n")) transistor_7 (.in(1'b0), .out(transistor_6_out), .gate(transistor_2_out));
  Transistor transistor_8 (.in(1'b1), .out(Y), .gate(C));
  Transistor #(.\type ("n")) transistor_9 (.in(transistor_10_out), .out(Y), .gate(transistor_6_out));
  Transistor #(.\type ("n")) transistor_10 (.in(1'b0), .out(transistor_10_out), .gate(C));
endmodule

module Exercise_184C (
  input  A,
  input  B,
  input  C,
  output Y
);

  wire transistor_1_out, transistor_4_out, transistor_5_out, transistor_7_out, transistor_8_out;

  Transistor transistor_1 (.in(1'b1), .out(transistor_1_out), .gate(B));
  Transistor transistor_2 (.in(1'b1), .out(transistor_1_out), .gate(A));
  Transistor #(.\type ("n")) transistor_3 (.in(transistor_4_out), .out(transistor_1_out), .gate(A));
  Transistor #(.\type ("n")) transistor_4 (.in(1'b0), .out(transistor_4_out), .gate(B));
  Transistor transistor_5 (.in(1'b1), .out(transistor_5_out), .gate(transistor_1_out));
  Transistor #(.\type ("n")) transistor_6 (.in(1'b0), .out(transistor_5_out), .gate(transistor_1_out));
  Transistor transistor_7 (.in(1'b1), .out(transistor_7_out), .gate(C));
  Transistor transistor_8 (.in(transistor_7_out), .out(transistor_8_out), .gate(transistor_5_out));
  Transistor #(.\type ("n")) transistor_9 (.in(1'b0), .out(transistor_8_out), .gate(C));
  Transistor #(.\type ("n")) transistor_10 (.in(1'b0), .out(transistor_8_out), .gate(transistor_5_out));
  Transistor transistor_11 (.in(1'b1), .out(Y), .gate(transistor_8_out));
  Transistor #(.\type ("n")) transistor_12 (.in(1'b0), .out(Y), .gate(transistor_8_out));
endmodule

module Exercise_185A (
  input  A,
  input  B,
  input  C,
  output Y
);

  wire transistor_3_out, transistor_4_out;

  Transistor #(.\type ("n")) transistor_1 (.in(1'b0), .out(Y), .gate(C));
  Transistor #(.\type ("n")) transistor_2 (.in(1'b0), .out(Y), .gate(B));
  Transistor transistor_3 (.in(1'b1), .out(transistor_3_out), .gate(A));
  Transistor transistor_4 (.in(transistor_3_out), .out(transistor_4_out), .gate(B));
  Transistor transistor_5 (.in(transistor_4_out), .out(Y), .gate(C));
  Transistor #(.\type ("n")) transistor_6 (.in(1'b0), .out(Y), .gate(A));
endmodule

module Exercise_185B (
  input  A,
  input  B,
  input  C,
  output Y
);

  wire transistor_1_out, transistor_7_out, transistor_8_out;

  Transistor transistor_1 (.in(1'b1), .out(transistor_1_out), .gate(C));
  Transistor transistor_2 (.in(1'b1), .out(transistor_1_out), .gate(B));
  Transistor transistor_3 (.in(1'b1), .out(transistor_1_out), .gate(A));
  Transistor #(.\type ("n")) transistor_4 (.in(transistor_7_out), .out(transistor_1_out), .gate(A));
  Transistor transistor_5 (.in(1'b1), .out(Y), .gate(transistor_1_out));
  Transistor #(.\type ("n")) transistor_6 (.in(1'b0), .out(Y), .gate(transistor_1_out));
  Transistor #(.\type ("n")) transistor_7 (.in(transistor_8_out), .out(transistor_7_out), .gate(B));
  Transistor #(.\type ("n")) transistor_8 (.in(1'b0), .out(transistor_8_out), .gate(C));
endmodule

module Exercise_185C (
  input  A,
  input  B,
  output Y
);

  wire transistor_1_out, transistor_2_out;

  Transistor transistor_1 (.in(1'b1), .out(transistor_1_out), .gate(A));
  Transistor transistor_2 (.in(transistor_1_out), .out(transistor_2_out), .gate(B));
  Transistor #(.\type ("n")) transistor_3 (.in(1'b0), .out(transistor_2_out), .gate(B));
  Transistor #(.\type ("n")) transistor_4 (.in(1'b0), .out(transistor_2_out), .gate(A));
  Transistor transistor_5 (.in(1'b1), .out(Y), .gate(transistor_2_out));
  Transistor #(.\type ("n")) transistor_6 (.in(1'b0), .out(Y), .gate(transistor_2_out));
endmodule

module Exercise_186 (
  input  A,
  input  B,
  input  C,
  output Y
);

  wire transistor_1_out, transistor_4_out, transistor_5_out, transistor_6_out, transistor_7_out;

  Transistor transistor_1 (.in(1'b1), .out(transistor_1_out), .gate(A));
  Transistor transistor_2 (.in(transistor_1_out), .out(Y), .gate(B));
  Transistor #(.\type ("n")) transistor_3 (.in(transistor_4_out), .out(Y), .gate(B));
  Transistor #(.\type ("n")) transistor_4 (.in(transistor_5_out), .out(transistor_4_out), .gate(B));
  Transistor #(.\type ("n")) transistor_5 (.in(1'b0), .out(transistor_5_out), .gate(C));
  Transistor transistor_6 (.in(1'b1), .out(transistor_6_out), .gate(B));
  Transistor transistor_7 (.in(1'b1), .out(transistor_7_out), .gate(A));
  Transistor transistor_8 (.in(transistor_6_out), .out(Y), .gate(C));
  Transistor transistor_9 (.in(transistor_7_out), .out(Y), .gate(C));
  Transistor #(.\type ("n")) transistor_10 (.in(transistor_4_out), .out(Y), .gate(A));
  Transistor #(.\type ("n")) transistor_11 (.in(transistor_5_out), .out(transistor_4_out), .gate(C));
  Transistor #(.\type ("n")) transistor_12 (.in(1'b0), .out(transistor_5_out), .gate(A));
endmodule

module Exercise_189A (
  input  A,
  input  B,
  input  C,
  output Y
);

  Transistor #(.\type ("n")) transistor_1 (.in(1'b0), .out(Y), .gate(A));
  Transistor transistor_2 (.in(1'b1), .out(Y), .gate(1'b0));
  Transistor #(.\type ("n")) transistor_3 (.in(1'b0), .out(Y), .gate(C));
  Transistor #(.\type ("n")) transistor_4 (.in(1'b0), .out(Y), .gate(B));
endmodule

module Exercise_189B (
  input  A,
  input  B,
  output Y
);

  wire transistor_1_out, transistor_5_out;

  Transistor transistor_1 (.in(1'b1), .out(transistor_1_out), .gate(1'b0));
  Transistor transistor_2 (.in(1'b1), .out(Y), .gate(transistor_1_out));
  Transistor #(.\type ("n")) transistor_3 (.in(transistor_5_out), .out(transistor_1_out), .gate(A));
  Transistor #(.\type ("n")) transistor_4 (.in(1'b0), .out(Y), .gate(transistor_1_out));
  Transistor #(.\type ("n")) transistor_5 (.in(1'b0), .out(transistor_5_out), .gate(B));
endmodule

module Exercise_189C (
  input  A,
  input  B,
  input  C,
  output Y
);

  wire transistor_3_out, transistor_4_out;

  Transistor transistor_1 (.in(1'b1), .out(Y), .gate(1'b0));
  Transistor #(.\type ("n")) transistor_2 (.in(transistor_3_out), .out(Y), .gate(A));
  Transistor #(.\type ("n")) transistor_3 (.in(transistor_4_out), .out(transistor_3_out), .gate(B));
  Transistor #(.\type ("n")) transistor_4 (.in(1'b0), .out(transistor_4_out), .gate(C));
endmodule

module Exercise_190 (
  input  A,
  input  B,
  input  C,
  output Y
);

  Transistor #(.\type ("n")) transistor_1 (.in(1'b0), .out(Y), .gate(A));
  Pull_Resistor #(.pull(1)) pull_resistor_1 (.node(Y));
  Transistor #(.\type ("n")) transistor_2 (.in(1'b0), .out(Y), .gate(C));
  Transistor #(.\type ("n")) transistor_3 (.in(1'b0), .out(Y), .gate(B));
endmodule
