// Logisim project Logic_Gates.circ as structural Verilog: 6 circuits, main circuit Exercise_171A
module Exercise_171A (
  input  A,
  input  B,
  input  C,
  output Y
);

  or or_1 (Y, A, B, C);
endmodule

module Exercise_171B (
  input  A,
  input  B,
  input  C,
  output Y
);

  xor xor_1 (Y, A, B, C);
endmodule

module Exercise_171C (
  input  A,
  input  B,
  input  C,
  input  D,
  output Y
);

  NotExactlyOne xnor_1 (.out(Y), .in0(A), .in1(B), .in2(C), .in3(D));
endmodule

module Exercise_172A (
  input  A,
  input  B,
  input  C,
  input  D,
  output Y
);

  or or_1 (Y, A, B, C, D);
endmodule

module Exercise_172B (
  input  A,
  input  B,
  input  C,
  output Y
);

  xnor xnor_1 (Y, A, B, C);
endmodule

module Exercise_172C (
  input  A,
  input  B,
  input  C,
  input  D,
  input  E,
  output Y
);

  nand nand_1 (Y, A, B, C, D, E);
endmodule
