// Logisim project Boolan_Equations.circ as structural Verilog: 30 circuits, main circuit Exercise_27A
module Exercise_27A (
  input  A,
  input  B,
  output Y
);

  wire not_1_out;

  or or_1 (Y, A, not_1_out);
  not not_1 (not_1_out, B);
endmodule

module Exercise_27B (
  input  A,
  input  B,
  input  C,
  output Y
);

  wire and_1_out, and_2_out, not_1_out, not_2_out, not_3_out;

  not not_1 (not_1_out, A);
  not not_2 (not_2_out, B);
  and and_1 (and_1_out, not_1_out, not_2_out, not_3_out);
  not not_3 (not_3_out, C);
  and and_2 (and_2_out, A, B, C);
  or or_1 (Y, and_1_out, and_2_out);
endmodule

module Exercise_27C (
  input  A,
  input  B,
  input  C,
  output Y
);

  wire and_1_out, not_1_out, not_2_out, xnor_1_out;

  not not_1 (not_1_out, B);
  not not_2 (not_2_out, C);
  and and_1 (and_1_out, not_1_out, not_2_out);
  or or_1 (Y, and_1_out, xnor_1_out);
  xnor xnor_1 (xnor_1_out, A, C);
endmodule

module Exercise_27D (
  input  A,
  input  B,
  input  C,
  input  D,
  output Y
);

  wire and_1_out, and_2_out, and_3_out, not_1_out, not_2_out, not_3_out;

  not not_1 (not_1_out, A);
  not not_2 (not_2_out, B);
  not not_3 (not_3_out, D);
  and and_1 (and_1_out, not_1_out, not_2_out);
  and and_2 (and_2_out, not_2_out, not_3_out);
  or or_1 (Y, and_1_out, and_2_out, and_3_out);
  and and_3 (and_3_out, not_3_out, A, C);
endmodule

module Exercise_27E (
  input  A,
  input  B,
  input  C,
  input  D,
  output Y
);

  wire xnor_1_out, xnor_2_out;

  xnor xnor_1 (xnor_1_out, A, B);
  xnor xnor_2 (xnor_2_out, C, D);
  xnor xnor_3 (Y, xnor_1_out, xnor_2_out);
endmodule

module Exercise_28A (
  input  A,
  input  B,
  output Y
);

  or or_1 (Y, A, B);
endmodule

module Exercise_28B (
  input  A,
  input  B,
  input  C,
  output Y
);

  wire and_1_out, not_1_out, xor_1_out;

  not not_1 (not_1_out, A);
  and and_1 (and_1_out, not_1_out, B);
  xor xor_1 (xor_1_out, C, A);
  or or_1 (Y, and_1_out, xor_1_out);
endmodule

module Exercise_28C (
  input  A,
  input  B,
  input  C,
  output Y
);

  wire and_1_out, and_2_out, not_1_out, not_2_out;

  and and_1 (and_1_out, A, B);
  not not_1 (not_1_out, A);
  and and_2 (and_2_out, C, not_1_out, not_2_out);
  not not_2 (not_2_out, B);
  or or_1 (Y, and_1_out, and_2_out);
endmodule

module Exercise_28D (
  input  A,
  input  B,
  input  C,
  input  D,
  output Y
);

  wire and_1_out, and_2_out, not_1_out, not_2_out, not_3_out;

  not not_1 (not_1_out, A);
  not not_2 (not_2_out, B);
  not not_3 (not_3_out, D);
  and and_1 (and_1_out, not_1_out, C);
  or or_1 (Y, and_1_out, and_2_out);
  and and_2 (and_2_out, not_2_out, not_3_out);
endmodule

module Exercise_28E (
  input  A,
  input  B,
  input  C,
  input  D,
  output Y
);

  wire and_1_out, and_2_out, and_3_out, not_1_out, not_2_out;

  not not_1 (not_1_out, A);
  not not_2 (not_2_out, B);
  and and_1 (and_1_out, not_1_out, B, C);
  and and_2 (and_2_out, not_1_out, C, D);
  or or_1 (Y, and_1_out, and_2_out, and_3_out);
  and and_3 (and_3_out, A, not_2_out);
endmodule

module Exercise_29A (
  input  A,
  input  B,
  output Y
);

  wire not_1_out;

  or or_1 (Y, A, not_1_out);
  not not_1 (not_1_out, B);
endmodule

module Exercise_29B (
  input  A,
  input  B,
  input  C,
  output Y
);

  wire and_1_out, and_2_out, not_1_out, not_2_out, not_3_out;

  not not_1 (not_1_out, A);
  not not_2 (not_2_out, B);
  and and_1 (and_1_out, not_1_out, not_2_out, not_3_out);
  not not_3 (not_3_out, C);
  and and_2 (and_2_out, A, B, C);
  or or_1 (Y, and_1_out, and_2_out);
endmodule

module Exercise_29C (
  input  A,
  input  B,
  input  C,
  output Y
);

  wire and_1_out, and_2_out, and_3_out, not_1_out, not_2_out, not_3_out;

  not not_1 (not_1_out, B);
  not not_2 (not_2_out, C);
  not not_3 (not_3_out, A);
  and and_1 (and_1_out, not_1_out, not_2_out);
  and and_2 (and_2_out, not_3_out, not_2_out);
  or or_1 (Y, and_1_out, and_2_out, and_3_out);
  and and_3 (and_3_out, A, C);
endmodule

module Exercise_29D (
  input  A,
  input  B,
  input  C,
  input  D,
  output Y
);

  wire and_1_out, and_2_out, and_3_out, not_1_out, not_2_out, not_3_out;

  not not_1 (not_1_out, A);
  not not_2 (not_2_out, B);
  not not_3 (not_3_out, D);
  and and_1 (and_1_out, not_1_out, not_2_out);
  and and_2 (and_2_out, not_2_out, not_3_out);
  or or_1 (Y, and_1_out, and_2_out, and_3_out);
  and and_3 (and_3_out, not_3_out, A, C);
endmodule

module Exercise_29E (
  input  A,
  input  B,
  input  C,
  input  D,
  output Y
);

  wire and_1_out, and_2_out, and_3_out, and_4_out, and_5_out, and_6_out, and_7_out, and_8_out, and_9_out,
       and_10_out, not_1_out, not_2_out, not_3_out, not_4_out, or_1_out, or_2_out, or_3_out, or_4_out;

  not not_1 (not_1_out, A);
  not not_2 (not_2_out, B);
  not not_3 (not_3_out, C);
  not not_4 (not_4_out, D);
  and and_1 (and_1_out, A, B);
  and and_2 (and_2_out, not_1_out, not_2_out);
  and and_3 (and_3_out, C, D);
  and and_4 (and_4_out, not_3_out, not_4_out);
  and and_5 (and_5_out, A, not_2_out);
  and and_6 (and_6_out, not_1_out, B);
  and and_7 (and_7_out, C, not_4_out);
  and and_8 (and_8_out, D, not_3_out);
  or or_1 (or_1_out, and_1_out, and_2_out);
  and and_9 (and_9_out, or_1_out, or_2_out);
  or or_2 (or_2_out, and_3_out, and_4_out);
  or or_3 (or_3_out, and_5_out, and_6_out);
  and and_10 (and_10_out, or_3_out, or_4_out);
  or or_4 (or_4_out, and_7_out, and_8_out);
  or or_5 (Y, and_9_out, and_10_out);
endmodule

module Exercise_210A (
  input  A,
  input  B,
  output Y
);

  or or_1 (Y, A, B);
endmodule

module Exercise_210B (
  input  A,
  input  B,
  input  C,
  output Y
);

  wire and_1_out, and_2_out, and_3_out, not_1_out, not_2_out;

  not not_1 (not_1_out, A);
  not not_2 (not_2_out, C);
  and and_1 (and_1_out, not_1_out, B);
  and and_2 (and_2_out, not_1_out, C);
  or or_1 (Y, and_1_out, and_2_out, and_3_out);
  and and_3 (and_3_out, A, not_2_out);
endmodule

module Exercise_210C (
  input  A,
  input  B,
  input  C,
  output Y
);

  wire and_1_out, and_2_out, not_1_out, not_2_out;

  and and_1 (and_1_out, A, B);
  not not_1 (not_1_out, A);
  and and_2 (and_2_out, C, not_1_out, not_2_out);
  not not_2 (not_2_out, B);
  or or_1 (Y, and_1_out, and_2_out);
endmodule

module Exercise_210D (
  input  A,
  input  B,
  input  C,
  input  D,
  output Y
);

  wire and_1_out, and_2_out, not_1_out, not_2_out, not_3_out;

  not not_1 (not_1_out, A);
  not not_2 (not_2_out, B);
  not not_3 (not_3_out, D);
  and and_1 (and_1_out, not_1_out, C);
  or or_1 (Y, and_1_out, and_2_out);
  and and_2 (and_2_out, not_2_out, not_3_out);
endmodule

module Exercise_210E (
  input  A,
  input  B,
  input  C,
  input  D,
  output Y
);

  wire and_1_out, and_2_out, and_3_out, not_1_out, not_2_out;

  not not_1 (not_1_out, A);
  not not_2 (not_2_out, B);
  and and_1 (and_1_out, not_1_out, B, C);
  and and_2 (and_2_out, not_1_out, C, D);
  or or_1 (Y, and_1_out, and_2_out, and_3_out);
  and and_3 (and_3_out, A, not_2_out);
endmodule

module Exercise_211A (
  input  A,
  input  B,
  output Y
);

  wire not_1_out;

  not not_1 (not_1_out, A);
  nand nand_1 (Y, not_1_out, B);
endmodule

module Exercise_211B (
  input  A,
  input  B,
  input  C,
  output Y
);

  wire nand_1_out, nand_3_out, not_1_out, not_2_out, not_3_out;

  not not_1 (not_1_out, A);
  not not_2 (not_2_out, B);
  not not_3 (not_3_out, C);
  nand nand_1 (nand_1_out, not_1_out, not_2_out, not_3_out);
  nand nand_2 (Y, nand_1_out, nand_3_out);
  nand nand_3 (nand_3_out, A, B, C);
endmodule

module Exercise_211C (
  input  A,
  input  B,
  input  C,
  output Y
);

  wire nand_1_out, nand_2_out, nand_4_out, not_1_out, not_2_out, not_3_out;

  not not_1 (not_1_out, B);
  not not_2 (not_2_out, C);
  not not_3 (not_3_out, A);
  nand nand_1 (nand_1_out, not_1_out, not_2_out);
  nand nand_2 (nand_2_out, not_3_out, not_2_out);
  nand nand_3 (Y, nand_1_out, nand_2_out, nand_4_out);
  nand nand_4 (nand_4_out, A, C);
endmodule

module Exercise_211D (
  input  A,
  input  B,
  input  C,
  input  D,
  output Y
);

  wire nand_1_out, nand_2_out, nand_3_out, not_1_out, not_2_out, not_3_out;

  not not_1 (not_1_out, A);
  not not_2 (not_2_out, B);
  not not_3 (not_3_out, D);
  nand nand_1 (nand_1_out, not_1_out, not_2_out);
  nand nand_2 (nand_2_out, not_2_out, not_3_out);
  nand nand_3 (nand_3_out, not_3_out, A, C);
  nand nand_4 (Y, nand_1_out, nand_2_out, nand_3_out);
endmodule

module Exercise_211E (
  input  A,
  input  B,
  input  C,
  input  D,
  output Y
);

  wire nand_1_out, nand_2_out, nand_3_out, nand_4_out, nand_5_out, nand_6_out, nand_7_out, nand_8_out,
       nand_9_out, nand_10_out, nand_11_out, nand_12_out, nand_13_out, nand_15_out, not_1_out, not_2_out,
       not_3_out, not_4_out;

  not not_1 (not_1_out, A);
  not not_2 (not_2_out, B);
  not not_3 (not_3_out, C);
  not not_4 (not_4_out, D);
  nand nand_1 (nand_1_out, A, B);
  nand nand_2 (nand_2_out, not_1_out, not_2_out);
  nand nand_3 (nand_3_out, C, D);
  nand nand_4 (nand_4_out, not_3_out, not_4_out);
  nand nand_5 (nand_5_out, A, not_2_out);
  nand nand_6 (nand_6_out, not_1_out, B);
  nand nand_7 (nand_7_out, C, not_4_out);
  nand nand_8 (nand_8_out, D, not_3_out);
  nand nand_9 (nand_9_out, nand_1_out, nand_2_out);
  nand nand_10 (nand_10_out, nand_3_out, nand_4_out);
  nand nand_11 (nand_11_out, nand_5_out, nand_6_out);
  nand nand_12 (nand_12_out, nand_7_out, nand_8_out);
  nand nand_13 (nand_13_out, nand_9_out, nand_10_out);
  nand nand_14 (Y, nand_13_out, nand_15_out);
  nand nand_15 (nand_15_out, nand_11_out, nand_12_out);
endmodule

module Exercise_212A (
  input  A,
  input  B,
  output Y
);

  wire not_1_out, not_2_out;

  not not_1 (not_1_out, A);
  nand nand_1 (Y, not_1_out, not_2_out);
  not not_2 (not_2_out, B);
endmodule

module Exercise_212B (
  input  A,
  input  B,
  input  C,
  output Y
);

  wire nand_1_out, nand_2_out, nand_4_out, not_1_out, not_2_out;

  not not_1 (not_1_out, A);
  not not_2 (not_2_out, C);
  nand nand_1 (nand_1_out, not_1_out, B);
  nand nand_2 (nand_2_out, not_1_out, C);
  nand nand_3 (Y, nand_1_out, nand_2_out, nand_4_out);
  nand nand_4 (nand_4_out, A, not_2_out);
endmodule

module Exercise_212C (
  input  A,
  input  B,
  input  C,
  output Y
);

  wire nand_1_out, nand_3_out, not_1_out, not_2_out;

  not not_1 (not_1_out, A);
  not not_2 (not_2_out, B);
  nand nand_1 (nand_1_out, A, B);
  nand nand_2 (Y, nand_1_out, nand_3_out);
  nand nand_3 (nand_3_out, C, not_1_out, not_2_out);
endmodule

module Exercise_212D (
  input  A,
  input  B,
  input  C,
  input  D,
  output Y
);

  wire nand_1_out, nand_3_out, not_1_out, not_2_out, not_3_out;

  not not_1 (not_1_out, A);
  not not_2 (not_2_out, B);
  not not_3 (not_3_out, D);
  nand nand_1 (nand_1_out, not_1_out, C);
  nand nand_2 (Y, nand_1_out, nand_3_out);
  nand nand_3 (nand_3_out, not_2_out, not_3_out);
endmodule

module Exercise_212E (
  input  A,
  input  B,
  input  C,
  input  D,
  output Y
);

  wire nand_1_out, nand_2_out, nand_3_out, not_1_out, not_2_out;

  not not_1 (not_1_out, A);
  not not_2 (not_2_out, B);
  nand nand_1 (nand_1_out, not_1_out, B, C);
  nand nand_2 (nand_2_out, not_1_out, C, D);
  nand nand_3 (nand_3_out, A, not_2_out);
  nand nand_4 (Y, nand_1_out, nand_2_out, nand_3_out);
endmodule
