// Logisim project Bubble_Pushing.circ as structural Verilog: 2 circuits, main circuit Exercise_226
module Exercise_226 (
  input  A,
  input  B,
  input  C,
  input  D,
  input  E,
  output Y
);

  wire and_1_out, or_1_out, or_2_out;

  or or_1 (or_1_out, ~A, ~B);  // OR_Gate
  and and_1 (and_1_out, or_1_out, or_2_out);
  or or_2 (or_2_out, ~C, ~D);  // OR_Gate
  or or_3 (Y, and_1_out, ~E);  // OR_Gate
endmodule

module Exercise_227 (
  input  A,
  input  B,
  input  C,
  input  D,
  input  E,
  input  F,
  input  G,
  output Y
);

  wire and_1_out, and_2_out, or_1_out, or_2_out;

  and and_1 (and_1_out, A, B, C);
  or or_1 (or_1_out, and_1_out, ~D);  // OR_Gate
  and and_2 (and_2_out, ~E, or_2_out);  // AND_Gate
  or or_2 (or_2_out, ~F, ~G);  // OR_Gate
  or or_3 (Y, or_1_out, and_2_out);
endmodule
