// Logisim project CMOS_Boolean_Equations.circ as structural Verilog: 6 circuits, main circuit Exercise_249A
module Exercise_249A (
  input  A,
  input  B,
  input  C,
  input  D,
  output W
);

  wire not_1_out, not_2_out, not_3_out, not_4_out, transistor_2_out, transistor_3_out, transistor_9_out,
       transistor_10_out;

  not not_1 (not_1_out, A);
  not not_2 (not_2_out, B);
  not not_3 (not_3_out, C);
  not not_4 (not_4_out, D);
  Transistor #(.\type ("n")) transistor_1 (.in(1'b0), .out(W), .gate(A));
  Transistor transistor_2 (.in(1'b1), .out(transistor_2_out), .gate(A));
  Transistor transistor_3 (.in(transistor_2_out), .out(transistor_3_out), .gate(B));
  Transistor transistor_4 (.in(transistor_2_out), .out(transistor_3_out), .gate(C));
  Transistor transistor_5 (.in(transistor_3_out), .out(W), .gate(D));
  Transistor transistor_6 (.in(transistor_3_out), .out(W), .gate(not_3_out));
  Transistor #(.\type ("n")) transistor_7 (.in(transistor_9_out), .out(W), .gate(B));
  Transistor #(.\type ("n")) transistor_8 (.in(transistor_10_out), .out(W), .gate(not_3_out));
  Transistor #(.\type ("n")) transistor_9 (.in(1'b0), .out(transistor_9_out), .gate(C));
  Transistor #(.\type ("n")) transistor_10 (.in(1'b0), .out(transistor_10_out), .gate(D));
endmodule

module Exercise_249B (
  input  A,
  input  B,
  input  C,
  input  D,
  output X
);

  wire not_1_out, not_2_out, not_3_out, not_4_out, transistor_1_out, transistor_2_out, transistor_3_out,
       transistor_4_out, transistor_12_out;

  not not_1 (not_1_out, A);
  not not_2 (not_2_out, B);
  not not_3 (not_3_out, C);
  not not_4 (not_4_out, D);
  Transistor #(.\type ("n")) transistor_1 (.in(1'b0), .out(transistor_1_out), .gate(B));
  Transistor transistor_2 (.in(1'b1), .out(transistor_2_out), .gate(A));
  Transistor transistor_3 (.in(transistor_2_out), .out(transistor_3_out), .gate(B));
  Transistor transistor_4 (.in(transistor_3_out), .out(transistor_4_out), .gate(C));
  Transistor transistor_5 (.in(transistor_4_out), .out(X), .gate(D));
  Transistor #(.\type ("n")) transistor_6 (.in(transistor_1_out), .out(X), .gate(not_1_out));
  Transistor #(.\type ("n")) transistor_7 (.in(1'b0), .out(transistor_1_out), .gate(C));
  Transistor #(.\type ("n")) transistor_8 (.in(1'b0), .out(transistor_1_out), .gate(D));
  Transistor transistor_9 (.in(1'b1), .out(transistor_2_out), .gate(not_4_out));
  Transistor transistor_10 (.in(transistor_2_out), .out(X), .gate(not_1_out));
  Transistor #(.\type ("n")) transistor_11 (.in(transistor_12_out), .out(X), .gate(not_4_out));
  Transistor #(.\type ("n")) transistor_12 (.in(1'b0), .out(transistor_12_out), .gate(A));
endmodule

module Exercise_249C (
  input  A,
  input  B,
  input  C,
  output Y
);

  wire not_1_out, not_2_out, not_3_out, transistor_1_out, transistor_3_out, transistor_8_out,
       transistor_10_out, transistor_11_out, transistor_15_out, transistor_16_out;

  not not_1 (not_1_out, A);
  not not_2 (not_2_out, B);
  not not_3 (not_3_out, C);
  Transistor transistor_1 (.in(1'b1), .out(transistor_1_out), .gate(A));
  Transistor transistor_2 (.in(1'b1), .out(transistor_1_out), .gate(not_2_out));
  Transistor transistor_3 (.in(transistor_1_out), .out(transistor_3_out), .gate(B));
  Transistor transistor_4 (.in(transistor_1_out), .out(transistor_3_out), .gate(C));
  Transistor transistor_5 (.in(transistor_3_out), .out(Y), .gate(not_2_out));
  Transistor transistor_6 (.in(transistor_3_out), .out(Y), .gate(not_3_out));
  Transistor #(.\type ("n")) transistor_7 (.in(transistor_8_out), .out(Y), .gate(not_1_out));
  Transistor #(.\type ("n")) transistor_8 (.in(transistor_10_out), .out(transistor_8_out), .gate(C));
  Transistor #(.\type ("n")) transistor_9 (.in(transistor_11_out), .out(transistor_8_out), .gate(not_3_out));
  Transistor #(.\type ("n")) transistor_10 (.in(1'b0), .out(transistor_10_out), .gate(B));
  Transistor #(.\type ("n")) transistor_11 (.in(1'b0), .out(transistor_11_out), .gate(not_2_out));
  Transistor transistor_12 (.in(1'b1), .out(transistor_1_out), .gate(C));
  Transistor transistor_13 (.in(transistor_1_out), .out(Y), .gate(not_1_out));
  Transistor #(.\type ("n")) transistor_14 (.in(transistor_15_out), .out(Y), .gate(A));
  Transistor #(.\type ("n")) transistor_15 (.in(transistor_16_out), .out(transistor_15_out), .gate(not_2_out));
  Transistor #(.\type ("n")) transistor_16 (.in(1'b0), .out(transistor_16_out), .gate(C));
endmodule

module Exercise_250A (
  input  A,
  input  B,
  input  C,
  input  D,
  output W
);

  wire not_1_out, not_2_out, not_3_out, not_4_out, transistor_1_out, transistor_4_out, transistor_5_out;

  Transistor transistor_1 (.in(1'b1), .out(transistor_1_out), .gate(D));
  Transistor transistor_2 (.in(transistor_1_out), .out(W), .gate(C));
  not not_1 (not_1_out, A);
  not not_2 (not_2_out, B);
  not not_3 (not_3_out, C);
  not not_4 (not_4_out, D);
  Transistor #(.\type ("n")) transistor_3 (.in(transistor_4_out), .out(W), .gate(A));
  Transistor #(.\type ("n")) transistor_4 (.in(1'b0), .out(transistor_4_out), .gate(D));
  Transistor transistor_5 (.in(1'b1), .out(transistor_5_out), .gate(B));
  Transistor transistor_6 (.in(transistor_5_out), .out(W), .gate(A));
  Transistor #(.\type ("n")) transistor_7 (.in(transistor_4_out), .out(W), .gate(B));
  Transistor #(.\type ("n")) transistor_8 (.in(1'b0), .out(transistor_4_out), .gate(C));
endmodule

module Exercise_250B (
  input  A,
  input  B,
  input  C,
  input  D,
  output X
);

  wire not_1_out, not_2_out, not_3_out, not_4_out, transistor_2_out, transistor_3_out, transistor_6_out,
       transistor_9_out, transistor_12_out;

  Transistor transistor_1 (.in(transistor_3_out), .out(X), .gate(not_1_out));
  not not_1 (not_1_out, A);
  not not_2 (not_2_out, B);
  not not_3 (not_3_out, C);
  not not_4 (not_4_out, D);
  Transistor #(.\type ("n")) transistor_2 (.in(1'b0), .out(transistor_2_out), .gate(D));
  Transistor transistor_3 (.in(1'b1), .out(transistor_3_out), .gate(A));
  Transistor transistor_4 (.in(transistor_3_out), .out(X), .gate(B));
  Transistor #(.\type ("n")) transistor_5 (.in(transistor_6_out), .out(X), .gate(B));
  Transistor #(.\type ("n")) transistor_6 (.in(transistor_2_out), .out(transistor_6_out), .gate(not_1_out));
  Transistor #(.\type ("n")) transistor_7 (.in(1'b0), .out(transistor_2_out), .gate(C));
  Transistor transistor_8 (.in(1'b1), .out(transistor_3_out), .gate(not_4_out));
  Transistor transistor_9 (.in(transistor_3_out), .out(transistor_9_out), .gate(D));
  Transistor transistor_10 (.in(transistor_9_out), .out(X), .gate(C));
  Transistor #(.\type ("n")) transistor_11 (.in(transistor_12_out), .out(X), .gate(not_4_out));
  Transistor #(.\type ("n")) transistor_12 (.in(1'b0), .out(transistor_12_out), .gate(A));
endmodule

module Exercise_250C (
  input  A,
  input  B,
  input  C,
  input  D,
  output Y
);

  wire not_1_out, not_2_out, not_3_out, not_4_out, transistor_1_out, transistor_4_out, transistor_5_out,
       transistor_8_out, transistor_14_out, transistor_15_out, transistor_16_out;

  Transistor transistor_1 (.in(1'b1), .out(transistor_1_out), .gate(A));
  not not_1 (not_1_out, A);
  not not_2 (not_2_out, B);
  not not_3 (not_3_out, C);
  not not_4 (not_4_out, D);
  Transistor transistor_2 (.in(1'b1), .out(transistor_1_out), .gate(not_2_out));
  Transistor transistor_3 (.in(transistor_8_out), .out(Y), .gate(not_3_out));
  Transistor #(.\type ("n")) transistor_4 (.in(transistor_5_out), .out(transistor_4_out), .gate(not_3_out));
  Transistor #(.\type ("n")) transistor_5 (.in(1'b0), .out(transistor_5_out), .gate(D));
  Transistor transistor_6 (.in(1'b1), .out(transistor_1_out), .gate(C));
  Transistor transistor_7 (.in(1'b1), .out(transistor_1_out), .gate(D));
  Transistor transistor_8 (.in(transistor_1_out), .out(transistor_8_out), .gate(B));
  Transistor transistor_9 (.in(transistor_1_out), .out(Y), .gate(not_1_out));
  Transistor transistor_10 (.in(transistor_8_out), .out(Y), .gate(D));
  Transistor #(.\type ("n")) transistor_11 (.in(transistor_4_out), .out(Y), .gate(not_1_out));
  Transistor #(.\type ("n")) transistor_12 (.in(transistor_14_out), .out(Y), .gate(A));
  Transistor #(.\type ("n")) transistor_13 (.in(1'b0), .out(transistor_4_out), .gate(B));
  Transistor #(.\type ("n")) transistor_14 (.in(transistor_15_out), .out(transistor_14_out), .gate(not_2_out));
  Transistor #(.\type ("n")) transistor_15 (.in(transistor_16_out), .out(transistor_15_out), .gate(C));
  Transistor #(.\type ("n")) transistor_16 (.in(1'b0), .out(transistor_16_out), .gate(D));
endmodule
