// Logisim project Faster_Decoder_8_Bits.circ as structural Verilog: 1 circuit, main circuit Exercise_245
module Exercise_245 (
  input  A2,
  input  A1,
  input  A0,
  output Y7,
  output Y6,
  output Y5,
  output Y4,
  output Y3,
  output Y2,
  output Y1,
  output Y0
);

  wire not_1_out, not_2_out, not_3_out;

  not not_1 (not_1_out, A2);
  not not_2 (not_2_out, A1);
  not not_3 (not_3_out, A0);
  and and_1 (Y7, A2, A1, A0);
  and and_2 (Y6, A2, A1, not_3_out);
  and and_3 (Y5, A2, not_2_out, A0);
  and and_4 (Y4, A2, not_2_out, not_3_out);
  and and_5 (Y3, not_1_out, A1, A0);
  and and_6 (Y2, not_1_out, A1, not_3_out);
  and and_7 (Y1, not_1_out, not_2_out, A0);
  and and_8 (Y0, not_1_out, not_2_out, not_3_out);
endmodule
