// Logisim project Faster_Multiplexer_8.circ as structural Verilog: 1 circuit, main circuit Exercise_246
module Exercise_246 (
  input  A7,
  input  A6,
  input  A5,
  input  A4,
  input  A3,
  input  A2,
  input  A1,
  input  A0,
  input  S2,
  input  S1,
  input  S0,
  output Z
);

  wire and_1_out, and_2_out, and_3_out, and_4_out, and_5_out, and_6_out, and_7_out, and_8_out, and_9_out,
       and_10_out, and_11_out, and_12_out, and_13_out, and_14_out, and_15_out, and_16_out, and_17_out,
       and_18_out, and_19_out, and_20_out, and_21_out, and_22_out, and_23_out, and_24_out, not_1_out,
       not_2_out, not_3_out, or_1_out, or_2_out, or_3_out, or_5_out, or_6_out, or_7_out;

  not not_1 (not_1_out, S2);
  not not_2 (not_2_out, S1);
  not not_3 (not_3_out, S0);
  and and_1 (and_1_out, S2, S1);
  and and_2 (and_2_out, S0, A7);
  and and_3 (and_3_out, S2, S1);
  and and_4 (and_4_out, and_1_out, and_2_out);
  or or_1 (or_1_out, and_4_out, and_7_out);
  and and_5 (and_5_out, not_3_out, A6);
  and and_6 (and_6_out, S2, not_2_out);
  and and_7 (and_7_out, and_3_out, and_5_out);
  or or_2 (or_2_out, or_1_out, or_3_out);
  and and_8 (and_8_out, S0, A5);
  and and_9 (and_9_out, S2, not_2_out);
  and and_10 (and_10_out, and_6_out, and_8_out);
  or or_3 (or_3_out, and_10_out, and_13_out);
  and and_11 (and_11_out, not_3_out, A4);
  and and_12 (and_12_out, not_1_out, S1);
  and and_13 (and_13_out, and_9_out, and_11_out);
  or or_4 (Z, or_2_out, or_6_out);
  and and_14 (and_14_out, S0, A3);
  and and_15 (and_15_out, not_1_out, S1);
  and and_16 (and_16_out, and_12_out, and_14_out);
  or or_5 (or_5_out, and_16_out, and_19_out);
  and and_17 (and_17_out, not_3_out, A2);
  and and_18 (and_18_out, not_1_out, not_2_out);
  and and_19 (and_19_out, and_15_out, and_17_out);
  or or_6 (or_6_out, or_5_out, or_7_out);
  and and_20 (and_20_out, S0, A1);
  and and_21 (and_21_out, not_1_out, not_2_out);
  and and_22 (and_22_out, and_18_out, and_20_out);
  or or_7 (or_7_out, and_22_out, and_24_out);
  and and_23 (and_23_out, not_3_out, A0);
  and and_24 (and_24_out, and_21_out, and_23_out);
endmodule
