// Logisim project Faster_Prime_Division.circ as structural Verilog: 1 circuit, main circuit Exercise_247
module Exercise_247 (
  input  A3,
  input  A2,
  input  A1,
  input  A0,
  output P,
  output D
);

  wire and_1_out, and_2_out, and_3_out, and_4_out, and_5_out, and_6_out, nand_1_out, nand_2_out, nand_3_out,
       nand_4_out, nand_5_out, nand_6_out, not_1_out, not_2_out, not_3_out, not_4_out, or_1_out, xor_1_out,
       xor_2_out;

  not not_1 (not_1_out, A3);
  not not_2 (not_2_out, A2);
  not not_3 (not_3_out, A1);
  not not_4 (not_4_out, A0);
  and and_1 (and_1_out, A3, not_2_out);
  and and_2 (and_2_out, not_3_out, A0);
  and and_3 (and_3_out, not_1_out, A2);
  and and_4 (and_4_out, A1, not_4_out);
  nand nand_1 (nand_1_out, A2, not_3_out, A0);
  and and_5 (and_5_out, nand_1_out, nand_2_out);
  nand nand_2 (nand_2_out, not_1_out, A2, A0);
  nand nand_3 (nand_3_out, not_2_out, A1, A0);
  and and_6 (and_6_out, nand_3_out, nand_4_out);
  nand nand_4 (nand_4_out, not_1_out, not_2_out, A1);
  xor xor_1 (xor_1_out, A3, A2);
  or or_1 (or_1_out, xor_1_out, xor_2_out);
  xor xor_2 (xor_2_out, A1, A0);
  nand nand_5 (nand_5_out, and_1_out, and_2_out);
  nand nand_6 (nand_6_out, and_3_out, and_4_out);
  nand nand_7 (P, and_5_out, and_6_out);
  nand nand_8 (D, or_1_out, nand_5_out, nand_6_out);
endmodule
