// Logisim project Faster_Priority_Encoder.circ as structural Verilog: 1 circuit, main circuit Exercise_248
module Exercise_248 (
  input  A7,
  input  A6,
  input  A5,
  input  A4,
  input  A3,
  input  A2,
  input  A1,
  input  A0,
  output Y2,
  output Y1,
  output Y0,
  output NONE
);

  wire and_1_out, and_2_out, and_3_out, and_4_out, and_5_out, and_6_out, and_8_out, nand_1_out, nand_2_out,
       nor_1_out, nor_2_out, nor_3_out, nor_4_out, nor_5_out, nor_6_out, nor_7_out, nor_8_out, nor_9_out,
       nor_10_out;

  nor nor_1 (nor_1_out, A7, A6);
  nor nor_2 (nor_2_out, A5, A4);
  nand nand_1 (nand_1_out, A3, ~A5, ~A4);  // NAND_Gate
  nand nand_2 (nand_2_out, A2, ~A5, ~A4);  // NAND_Gate
  and and_1 (and_1_out, A5, ~A6);  // AND_Gate
  and and_2 (and_2_out, A3, ~A5, ~A4);  // AND_Gate
  and and_3 (and_3_out, A1, ~A6);  // AND_Gate
  nor nor_3 (nor_3_out, A4, A2);
  nor nor_4 (nor_4_out, A7, A6);
  nor nor_5 (nor_5_out, A5, A4);
  nor nor_6 (nor_6_out, A3, A2);
  nor nor_7 (nor_7_out, A1, A0);
  nand nand_3 (Y2, nor_1_out, nor_2_out);
  and and_4 (and_4_out, nand_1_out, nand_2_out);
  nand nand_4 (Y1, and_4_out, nor_8_out);
  nor nor_8 (nor_8_out, A7, A6);
  nor nor_9 (nor_9_out, A7, and_1_out);
  nor nor_10 (nor_10_out, and_2_out, and_5_out);
  and and_5 (and_5_out, and_3_out, nor_3_out);
  and and_6 (and_6_out, nor_4_out, nor_5_out);
  and and_7 (NONE, and_6_out, and_8_out);
  and and_8 (and_8_out, nor_6_out, nor_7_out);
  nand nand_5 (Y0, nor_9_out, nor_10_out);
endmodule
