// Logisim project K_Maps.circ as structural Verilog: 6 circuits, main circuit Exercise_215A
module Exercise_215A (
  input  A,
  input  B,
  input  C,
  output Y
);

  wire and_1_out, and_2_out;

  and and_1 (and_1_out, A, C);
  and and_2 (and_2_out, ~B, C);  // AND_Gate
  or or_1 (Y, and_1_out, and_2_out);
endmodule

module Exercise_215B (
  input  A,
  output Y
);

  not not_1 (Y, A);
endmodule

module Exercise_215C (
  input  A,
  input  B,
  input  C,
  input  D,
  output Y
);

  wire and_1_out, xnor_1_out;

  xnor xnor_1 (xnor_1_out, B, D);
  or or_1 (Y, ~A, xnor_1_out, and_1_out);  // OR_Gate
  and and_1 (and_1_out, ~C, D);  // AND_Gate
endmodule

module Exercise_216A (
  input  A,
  input  B,
  output Y
);

  and and_1 (Y, ~A, B);  // AND_Gate
endmodule

module Exercise_216B (
  input  A,
  input  B,
  input  C,
  output Y
);

  wire and_1_out, and_2_out;

  and and_1 (and_1_out, A, ~B);  // AND_Gate
  and and_2 (and_2_out, ~B, ~C);  // AND_Gate
  or or_1 (Y, and_1_out, and_2_out);
endmodule

module Exercise_216C (
  input  A,
  input  B,
  input  C,
  input  D,
  output Y
);

  wire and_1_out, and_2_out;

  and and_1 (and_1_out, A, B, C, ~D);  // AND_Gate
  or or_1 (Y, and_1_out, and_2_out);
  and and_2 (and_2_out, ~B, ~C, ~D);  // AND_Gate
endmodule
