// Logisim project K_Maps_X.circ as structural Verilog: 2 circuits, main circuit Exercise_229
module Exercise_229 (
  input  A,
  input  B,
  input  C,
  input  D,
  output Y
);

  wire and_1_out, and_2_out, and_3_out;

  and and_1 (and_1_out, A, B);
  and and_2 (and_2_out, C, A);
  and and_3 (and_3_out, A, ~D);  // AND_Gate
  or or_1 (Y, and_1_out, and_2_out, and_3_out);
endmodule

module Exercise_232 (
  input  A,
  input  B,
  input  C,
  input  D,
  output Y
);

  wire and_1_out, and_2_out, and_3_out, and_4_out;

  and and_1 (and_1_out, ~A, D);  // AND_Gate
  and and_2 (and_2_out, C, D);
  and and_3 (and_3_out, B, D);
  and and_4 (and_4_out, A, ~B, ~C, ~D);  // AND_Gate
  or or_1 (Y, and_1_out, and_2_out, and_3_out, and_4_out);
endmodule
