// Logisim project Multiplexer_Logic.circ as structural Verilog: 6 circuits, main circuit Exercise_241A
module Exercise_241A (
  input  A,
  input  B,
  input  C,
  output Y
);

  Multiplexer #(.select(3)) multiplexer_1 (
    .in0(1'b1), .in1(1'b0), .in2(1'b0), .in3(1'b0), .in4(1'b0), .in5(1'b0), .in6(1'b0), .in7(1'b1), .out(Y),
    .sel({A, B, C}));
endmodule

module Exercise_241B (
  input  A,
  input  B,
  input  C,
  output Y
);

  wire not_1_out;

  not not_1 (not_1_out, A);
  Multiplexer #(.select(2)) multiplexer_1 (.in0(not_1_out), .in1(1'b0), .in2(1'b0), .in3(A), .out(Y), .sel({B, C}));
endmodule

module Exercise_241C (
  input  A,
  input  B,
  input  C,
  output Y
);

  wire and_1_out, nor_1_out;

  nor nor_1 (nor_1_out, A, B);
  Multiplexer multiplexer_1 (.in0(nor_1_out), .in1(and_1_out), .out(Y), .sel(C));
  and and_1 (and_1_out, A, B);
endmodule

module Exercise_242A (
  input  A,
  input  B,
  input  C,
  output Y
);

  Multiplexer #(.select(3)) multiplexer_1 (
    .in0(1'b1), .in1(1'b0), .in2(1'b1), .in3(1'b1), .in4(1'b0), .in5(1'b0), .in6(1'b1), .in7(1'b1), .out(Y),
    .sel({A, B, C}));
endmodule

module Exercise_242B (
  input  B,
  input  A,
  input  C,
  output Y
);

  Multiplexer #(.select(2)) multiplexer_1 (.in0(1'b1), .in1(B), .in2(B), .in3(B), .out(Y), .sel({A, C}));
endmodule

module Exercise_242C (
  input  A,
  input  C,
  input  B,
  output Y
);

  wire nor_1_out;

  nor nor_1 (nor_1_out, A, C);
  Multiplexer multiplexer_1 (.in0(nor_1_out), .in1(1'b1), .out(Y), .sel(B));
endmodule
