// Logisim project Prime_Division.circ as structural Verilog: 1 circuit, main circuit Exercise_235
module Exercise_235 (
  input  A3,
  input  A2,
  input  A1,
  input  A0,
  output P,
  output D
);

  wire and_1_out, and_2_out, and_3_out, and_4_out, and_5_out, and_6_out, and_7_out, and_8_out, and_9_out,
       and_10_out;

  and and_1 (and_1_out, ~A3, ~A2, A1);  // AND_Gate
  and and_2 (and_2_out, A1, ~A2, A0);  // AND_Gate
  or or_1 (P, and_1_out, and_2_out, and_3_out, and_4_out);
  and and_3 (and_3_out, ~A3, A2, A0);  // AND_Gate
  and and_4 (and_4_out, A2, ~A1, A0);  // AND_Gate
  and and_5 (and_5_out, ~A3, ~A2, A1, A0);  // AND_Gate
  and and_6 (and_6_out, ~A3, A2, A1, ~A0);  // AND_Gate
  and and_7 (and_7_out, A3, ~A2, ~A1, A0);  // AND_Gate
  or or_2 (D, and_5_out, and_6_out, and_7_out, and_8_out, and_9_out, and_10_out);
  and and_8 (and_8_out, A3, A2, ~A1, ~A0);  // AND_Gate
  and and_9 (and_9_out, A3, A2, A1, A0);
  and and_10 (and_10_out, ~A3, ~A2, ~A1, ~A0);  // AND_Gate
endmodule
