// Logisim project Priority_Encoders.circ as structural Verilog: 2 circuits, main circuit Exercise_236
module Exercise_236 (
  input  A7,
  input  A6,
  input  A5,
  input  A4,
  input  A3,
  input  A2,
  input  A1,
  input  A0,
  output Y2,
  output Y1,
  output Y0,
  output NONE
);

  wire and_1_out, and_2_out, and_3_out, and_4_out, and_5_out;

  or or_1 (Y2, A7, A6, A5, A4);
  and and_1 (and_1_out, A3, ~A5, ~A4);  // AND_Gate
  and and_2 (and_2_out, A2, ~A5, ~A4);  // AND_Gate
  or or_2 (Y1, and_1_out, and_2_out, A7, A6);
  and and_3 (and_3_out, A5, ~A6);  // AND_Gate
  and and_4 (and_4_out, A3, ~A6, ~A4);  // AND_Gate
  and and_5 (and_5_out, A1, ~A6, ~A4, ~A2);  // AND_Gate
  and and_6 (NONE, ~A0, ~A7, ~A6, ~A5, ~A4, ~A3, ~A2, ~A1);  // AND_Gate
  or or_3 (Y0, A7, and_3_out, and_4_out, and_5_out);
endmodule

module Exercise_237 (
  input  A7,
  input  A6,
  input  A5,
  input  A4,
  input  A3,
  input  A2,
  input  A1,
  input  A0,
  output Z2,
  output Z1,
  output Z0,
  output NONE
);

  wire and_1_out, and_2_out, and_3_out, and_4_out, and_5_out, and_6_out, or_1_out, or_2_out, or_3_out,
       or_4_out, or_5_out, or_6_out;

  or or_1 (or_1_out, A7, A6);
  or or_2 (or_2_out, or_1_out, A5);
  or or_3 (or_3_out, or_2_out, A4);
  or or_4 (or_4_out, or_3_out, A3);
  or or_5 (or_5_out, or_4_out, A2);
  and and_1 (and_1_out, A7, A6);
  and and_2 (and_2_out, or_1_out, A5);
  and and_3 (and_3_out, or_2_out, A4);
  and and_4 (and_4_out, or_3_out, A3);
  and and_5 (and_5_out, or_4_out, A2);
  and and_6 (and_6_out, or_5_out, A1);
  or or_6 (or_6_out, or_5_out, A1);
  and and_7 (NONE, ~or_6_out, ~A0);  // AND_Gate
  or or_7 (Z2, and_1_out, and_2_out, and_3_out);
  or or_8 (Z1, and_1_out, and_4_out, and_5_out);
  or or_9 (Z0, and_2_out, and_4_out, and_6_out);
endmodule
