// Logisim project Seven_Segment_Display.circ as structural Verilog: 1 circuit, main circuit Exercise_234
module Exercise_234 (
  input  D3,
  input  D2,
  input  D1,
  input  D0,
  output SA,
  output SB,
  output SC,
  output SD,
  output SE,
  output SF,
  output SG
);

  wire and_1_out, and_2_out, and_3_out, and_4_out, and_5_out, and_6_out, and_7_out, and_8_out, and_9_out,
       and_10_out, and_11_out, and_12_out, and_13_out, and_14_out, and_15_out, and_16_out;

  and and_1 (and_1_out, D2, D0);
  or or_1 (SA, D3, and_1_out, and_2_out, D1);
  and and_2 (and_2_out, ~D0, ~D2);  // AND_Gate
  and and_3 (and_3_out, D1, D0);
  and and_4 (and_4_out, ~D1, ~D0);  // AND_Gate
  or or_2 (SB, and_3_out, and_4_out, ~D2);  // OR_Gate
  or or_3 (SC, D2, ~D1, D0);  // OR_Gate
  and and_5 (and_5_out, ~D2, ~D0);  // AND_Gate
  and and_6 (and_6_out, ~D2, D1);  // AND_Gate
  and and_7 (and_7_out, D1, ~D0);  // AND_Gate
  or or_4 (SD, and_5_out, and_6_out, and_7_out, and_8_out, D3);
  and and_8 (and_8_out, D2, ~D1, D0);  // AND_Gate
  and and_9 (and_9_out, ~D2, ~D0);  // AND_Gate
  or or_5 (SE, and_9_out, and_10_out);
  and and_10 (and_10_out, D1, ~D0);  // AND_Gate
  and and_11 (and_11_out, D2, ~D1);  // AND_Gate
  or or_6 (SF, D3, and_11_out, and_12_out, and_13_out);
  and and_12 (and_12_out, D2, ~D0);  // AND_Gate
  and and_13 (and_13_out, ~D1, ~D0);  // AND_Gate
  and and_14 (and_14_out, ~D2, D1);  // AND_Gate
  or or_7 (SG, D3, and_14_out, and_15_out, and_16_out);
  and and_15 (and_15_out, D2, ~D1);  // AND_Gate
  and and_16 (and_16_out, D1, ~D0);  // AND_Gate
endmodule
