// Logisim project Simplified_Equations.circ as structural Verilog: 7 circuits, main circuit Exercise_217A
module Exercise_217A (
  input  A,
  input  C,
  input  B,
  output Y
);

  wire and_1_out;

  and and_1 (and_1_out, ~A, ~C);  // AND_Gate
  or or_1 (Y, and_1_out, B);
endmodule

module Exercise_217B (
  input  A,
  input  B,
  output Y
);

  and and_1 (Y, ~A, B);  // AND_Gate
endmodule

module Exercise_217C (
  input  A,
  input  B,
  input  C,
  input  D,
  input  E,
  output Y
);

  wire and_1_out, and_2_out;

  and and_1 (and_1_out, ~B, ~C);  // AND_Gate
  or or_1 (Y, A, and_1_out, and_2_out);
  and and_2 (and_2_out, ~D, ~E);  // AND_Gate
endmodule

module Exercise_218A (
  input  B,
  input  C,
  output Y
);

  or or_1 (Y, ~B, C);  // OR_Gate
endmodule

module Exercise_218B (
  input  A,
  input  B,
  input  C,
  input  D,
  output Y
);

  wire and_1_out, and_2_out;

  and and_1 (and_1_out, A, D);
  and and_2 (and_2_out, ~C, D);  // AND_Gate
  or or_1 (Y, and_1_out, and_2_out, B);
endmodule

module Exercise_218C (
  input  A,
  input  B,
  input  C,
  input  D,
  input  E,
  output Y
);

  wire and_1_out, and_2_out, and_3_out;

  and and_1 (and_1_out, A, B, C, D);
  and and_2 (and_2_out, B, ~D, E);  // AND_Gate
  or or_1 (Y, and_1_out, and_2_out, and_3_out);
  and and_3 (and_3_out, ~A, B, ~C, D);  // AND_Gate
endmodule

module Exercise_225 (
  input  A,
  input  B,
  input  C,
  input  D,
  output Y,
  output Z
);

  wire and_1_out, and_2_out, and_3_out;

  and and_1 (and_1_out, A, ~B, C);  // AND_Gate
  and and_2 (and_2_out, A, ~C, D);  // AND_Gate
  and and_3 (and_3_out, B, D);
  or or_1 (Y, and_1_out, D);
  or or_2 (Z, and_2_out, and_3_out);
endmodule
