// Logisim project Thermomether_Decoder.circ as structural Verilog: 1 circuit, main circuit Exercise_238
module Exercise_238 (
  input  A2,
  input  A1,
  input  A0,
  output Y6,
  output Y5,
  output Y4,
  output Y3,
  output Y2,
  output Y1,
  output Y0
);

  wire and_4_out, or_1_out;

  and and_1 (Y5, A2, A1);
  and and_2 (Y6, A2, A1, A0);
  or or_1 (or_1_out, A1, A0);
  and and_3 (Y4, A2, or_1_out);
  and and_4 (and_4_out, A1, A0);
  or or_2 (Y1, A2, A1);
  or or_3 (Y2, and_4_out, A2);
  or or_4 (Y0, A2, A1, A0);

  assign Y3 = A2;
endmodule
