// Logisim project CLK_Analysis.circ as structural Verilog: 1 circuit, main circuit Exercise_333
module Exercise_333 (
  input  A,
  input  B,
  input  C,
  input  D,
  output Y
);

  wire CLK_out, d_ff_1_q, d_ff_2_q, d_ff_3_q, d_ff_4_q, xor_1_out, xor_2_out, xor_3_out;

  Clock CLK (.out(CLK_out));
  D_Flip_Flop d_ff_1 (.D(A), .clk(CLK_out), .Q(d_ff_1_q));  // open: Qn, preset, reset
  D_Flip_Flop d_ff_2 (.D(B), .clk(CLK_out), .Q(d_ff_2_q));  // open: Qn, preset, reset
  D_Flip_Flop d_ff_3 (.D(C), .clk(CLK_out), .Q(d_ff_3_q));  // open: Qn, preset, reset
  D_Flip_Flop d_ff_4 (.D(D), .clk(CLK_out), .Q(d_ff_4_q));  // open: Qn, preset, reset
  xor xor_1 (xor_1_out, d_ff_1_q, d_ff_2_q);
  xor xor_2 (xor_2_out, xor_1_out, xor_3_out);
  xor xor_3 (xor_3_out, d_ff_3_q, d_ff_4_q);
  D_Flip_Flop d_ff_5 (.D(xor_2_out), .clk(CLK_out), .Q(Y));  // open: Qn, preset, reset
endmodule
