// Logisim project FSM_Excercises.circ as structural Verilog: 9 circuits, main circuit Exercise_322
module Exercise_322 (
  input  A,
  input  B,
  input  RESET,
  output Q
);

  wire and_1_out, and_2_out, CLK_out, d_ff_1_q, d_ff_2_q;

  Clock CLK (.out(CLK_out));
  and and_1 (and_1_out, ~d_ff_1_q, d_ff_2_q, B);  // AND_Gate
  and and_2 (and_2_out, ~d_ff_1_q, ~d_ff_2_q, A);  // AND_Gate
  D_Flip_Flop d_ff_1 (.D(and_1_out), .clk(CLK_out), .Q(d_ff_1_q), .reset(RESET));  // open: Qn, preset
  D_Flip_Flop d_ff_2 (.D(and_2_out), .clk(CLK_out), .Q(d_ff_2_q), .reset(RESET));  // open: Qn, preset
  and and_3 (Q, d_ff_1_q, ~d_ff_2_q);  // AND_Gate
endmodule

module Exercise_323 (
  input  A,
  input  B,
  input  RESET,
  output Q
);

  wire and_1_out, and_2_out, and_3_out, CLK_out, d_ff_1_q, d_ff_2_q, or_1_out;

  Clock CLK (.out(CLK_out));
  and and_1 (and_1_out, ~d_ff_1_q, d_ff_2_q, B);  // AND_Gate
  and and_2 (and_2_out, d_ff_1_q, ~d_ff_2_q, A, B);  // AND_Gate
  D_Flip_Flop d_ff_1 (.D(or_1_out), .clk(CLK_out), .Q(d_ff_1_q), .reset(RESET));  // open: Qn, preset
  or or_1 (or_1_out, and_1_out, and_2_out);
  D_Flip_Flop d_ff_2 (.D(and_3_out), .clk(CLK_out), .Q(d_ff_2_q), .reset(RESET));  // open: Qn, preset
  and and_3 (and_3_out, ~d_ff_1_q, ~d_ff_2_q, A);  // AND_Gate
  and and_4 (Q, A, B, d_ff_1_q, ~d_ff_2_q);  // AND_Gate
endmodule

module Exercise_324 (
  input  TA,
  input  TB,
  input  RESET,
  output LA1,
  output LA0,
  output LB1,
  output LB0
);

  wire and_1_out, and_2_out, and_3_out, and_4_out, and_6_out, CLK_out, d_ff_1_q, d_ff_2_q, d_ff_3_q, or_1_out;

  Clock CLK (.out(CLK_out));
  and and_1 (and_1_out, d_ff_1_q, d_ff_2_q, d_ff_3_q, TB);
  and and_2 (and_2_out, ~d_ff_1_q, d_ff_3_q);  // AND_Gate
  or or_1 (or_1_out, and_1_out, and_2_out, and_3_out);
  and and_3 (and_3_out, ~d_ff_1_q, ~d_ff_2_q, ~d_ff_3_q, ~TA);  // AND_Gate
  D_Flip_Flop d_ff_1 (.D(d_ff_2_q), .clk(CLK_out), .Q(d_ff_1_q), .reset(RESET));  // open: Qn, preset
  D_Flip_Flop d_ff_2 (.D(d_ff_3_q), .clk(CLK_out), .Q(d_ff_2_q), .reset(RESET));  // open: Qn, preset
  D_Flip_Flop d_ff_3 (.D(or_1_out), .clk(CLK_out), .Q(d_ff_3_q), .reset(RESET));  // open: Qn, preset
  and and_4 (and_4_out, d_ff_2_q, d_ff_3_q);
  and and_5 (LA0, ~d_ff_1_q, ~d_ff_2_q, d_ff_3_q);  // AND_Gate
  and and_6 (and_6_out, ~d_ff_2_q, ~d_ff_3_q);  // AND_Gate
  and and_7 (LB0, d_ff_1_q, d_ff_2_q, ~d_ff_3_q);  // AND_Gate
  or or_2 (LA1, d_ff_1_q, and_4_out);
  or or_3 (LB1, ~d_ff_1_q, and_6_out);  // OR_Gate
endmodule

module Exercise_325 (
  input  A,
  input  RESET,
  output Y
);

  wire and_1_out, and_2_out, and_3_out, and_4_out, and_5_out, and_6_out, and_7_out, and_8_out, and_9_out,
       and_10_out, and_11_out, CLK_out, d_ff_1_q, d_ff_2_q, d_ff_3_q, or_1_out, or_2_out, or_3_out;

  and and_1 (and_1_out, ~d_ff_1_q, d_ff_2_q, ~d_ff_3_q, A);  // AND_Gate
  and and_2 (and_2_out, d_ff_1_q, ~d_ff_2_q, ~d_ff_3_q, A);  // AND_Gate
  and and_3 (and_3_out, ~d_ff_1_q, ~d_ff_2_q, d_ff_3_q, A);  // AND_Gate
  and and_4 (and_4_out, ~d_ff_1_q, d_ff_2_q, ~d_ff_3_q, ~A);  // AND_Gate
  and and_5 (and_5_out, d_ff_1_q, ~d_ff_2_q, ~d_ff_3_q, ~A);  // AND_Gate
  and and_6 (and_6_out, ~d_ff_1_q, ~d_ff_2_q, ~d_ff_3_q, A);  // AND_Gate
  and and_7 (and_7_out, ~d_ff_1_q, d_ff_2_q, ~d_ff_3_q, ~A);  // AND_Gate
  and and_8 (and_8_out, d_ff_1_q, ~d_ff_2_q, ~d_ff_3_q, ~A);  // AND_Gate
  and and_9 (and_9_out, ~d_ff_1_q, d_ff_2_q, d_ff_3_q, A);  // AND_Gate
  D_Flip_Flop d_ff_1 (.D(or_1_out), .clk(CLK_out), .Q(d_ff_1_q), .reset(RESET));  // open: Qn, preset
  or or_1 (or_1_out, and_1_out, and_2_out);
  D_Flip_Flop d_ff_2 (.D(or_2_out), .clk(CLK_out), .Q(d_ff_2_q), .reset(RESET));  // open: Qn, preset
  or or_2 (or_2_out, and_3_out, and_4_out, and_5_out);
  D_Flip_Flop d_ff_3 (.D(or_3_out), .clk(CLK_out), .Q(d_ff_3_q), .reset(RESET));  // open: Qn, preset
  or or_3 (or_3_out, and_6_out, and_7_out, and_8_out, and_9_out);
  Clock CLK (.out(CLK_out));
  and and_10 (and_10_out, ~d_ff_1_q, ~d_ff_2_q, d_ff_3_q, A);  // AND_Gate
  and and_11 (and_11_out, d_ff_1_q, ~d_ff_2_q, ~d_ff_3_q, ~A);  // AND_Gate
  or or_4 (Y, and_10_out, and_11_out);
endmodule

module Exercise_326 (
  input  N,
  input  D,
  input  Q,
  input  RESET,
  output DISP,
  output R2D,
  output RD,
  output RN
);

  wire and_1_out, and_2_out, and_3_out, and_4_out, and_5_out, and_6_out, and_7_out, and_8_out, and_9_out,
       and_10_out, and_11_out, and_12_out, and_13_out, and_14_out, and_15_out, CLK_out, d_ff_2_q, d_ff_3_q,
       d_ff_4_q, d_ff_5_q, d_ff_6_q, d_ff_7_q, d_ff_8_q, d_ff_9_q, d_ff_10_q, or_1_out, or_2_out, or_3_out,
       or_4_out, or_5_out, or_6_out;

  Clock CLK (.out(CLK_out));
  and and_1 (and_1_out, Q, d_ff_6_q);
  and and_2 (and_2_out, Q, d_ff_7_q);
  and and_3 (and_3_out, Q, d_ff_8_q);
  and and_4 (and_4_out, Q, d_ff_9_q);
  or or_1 (or_1_out, and_4_out, and_5_out);
  and and_5 (and_5_out, D, d_ff_6_q);
  and and_6 (and_6_out, Q, d_ff_10_q);
  and and_7 (and_7_out, D, d_ff_7_q);
  or or_2 (or_2_out, and_6_out, and_7_out, and_8_out);
  and and_8 (and_8_out, N, d_ff_6_q);
  and and_9 (and_9_out, D, d_ff_8_q);
  or or_3 (or_3_out, and_9_out, and_10_out);
  and and_10 (and_10_out, N, d_ff_7_q);
  and and_11 (and_11_out, D, d_ff_9_q);
  or or_4 (or_4_out, and_11_out, and_12_out);
  and and_12 (and_12_out, N, d_ff_8_q);
  and and_13 (and_13_out, D, d_ff_10_q);
  or or_5 (or_5_out, and_13_out, and_14_out);
  and and_14 (and_14_out, N, d_ff_9_q);
  and and_15 (and_15_out, N, d_ff_10_q);
  or or_6 (or_6_out, d_ff_5_q, d_ff_4_q, d_ff_3_q, d_ff_2_q, R2D);
  D_Flip_Flop d_ff_1 (.D(and_1_out), .clk(CLK_out), .Q(R2D), .reset(RESET));  // open: Qn, preset
  D_Flip_Flop d_ff_2 (.D(and_2_out), .clk(CLK_out), .Q(d_ff_2_q), .reset(RESET));  // open: Qn, preset
  D_Flip_Flop d_ff_3 (.D(and_3_out), .clk(CLK_out), .Q(d_ff_3_q), .reset(RESET));  // open: Qn, preset
  D_Flip_Flop d_ff_4 (.D(or_1_out), .clk(CLK_out), .Q(d_ff_4_q), .reset(RESET));  // open: Qn, preset
  D_Flip_Flop d_ff_5 (.D(or_2_out), .clk(CLK_out), .Q(d_ff_5_q), .reset(RESET));  // open: Qn, preset
  D_Flip_Flop d_ff_6 (.D(or_3_out), .clk(CLK_out), .Q(d_ff_6_q), .reset(RESET));  // open: Qn, preset
  D_Flip_Flop d_ff_7 (.D(or_4_out), .clk(CLK_out), .Q(d_ff_7_q), .reset(RESET));  // open: Qn, preset
  D_Flip_Flop d_ff_8 (.D(or_5_out), .clk(CLK_out), .Q(d_ff_8_q), .reset(RESET));  // open: Qn, preset
  D_Flip_Flop d_ff_9 (.D(and_15_out), .clk(CLK_out), .Q(d_ff_9_q), .reset(RESET));  // open: Qn, preset
  D_Flip_Flop d_ff_10 (.D(or_6_out), .clk(CLK_out), .Q(d_ff_10_q), .preset(RESET));  // open: Qn, reset
  or or_7 (DISP, R2D, d_ff_2_q, d_ff_3_q, d_ff_4_q, d_ff_5_q);
  or or_8 (RD, d_ff_2_q, d_ff_3_q);
  or or_9 (RN, d_ff_2_q, d_ff_4_q);
endmodule

module Exercise_327 (
  input  RESET,
  output Y2,
  output Y1,
  output Y0
);

  wire and_1_out, and_2_out, and_3_out, and_4_out, and_5_out, and_6_out, CLK_out, or_1_out, or_2_out,
       or_3_out;

  and and_1 (and_1_out, Y1, ~Y0);  // AND_Gate
  or or_1 (or_1_out, and_1_out, and_2_out);
  and and_2 (and_2_out, Y2, Y0);
  and and_3 (and_3_out, ~Y2, Y0);  // AND_Gate
  or or_2 (or_2_out, and_3_out, and_4_out);
  and and_4 (and_4_out, Y1, ~Y0);  // AND_Gate
  and and_5 (and_5_out, ~Y2, ~Y1);  // AND_Gate
  or or_3 (or_3_out, and_5_out, and_6_out);
  and and_6 (and_6_out, Y2, Y1);
  Clock CLK (.out(CLK_out));
  D_Flip_Flop d_ff_1 (.D(or_1_out), .clk(CLK_out), .Q(Y2), .reset(RESET));  // open: Qn, preset
  D_Flip_Flop d_ff_2 (.D(or_2_out), .clk(CLK_out), .Q(Y1), .reset(RESET));  // open: Qn, preset
  D_Flip_Flop d_ff_3 (.D(or_3_out), .clk(CLK_out), .Q(Y0), .reset(RESET));  // open: Qn, preset
endmodule

module Exercise_328 (
  input  UP,
  input  RESET,
  output Y2,
  output Y1,
  output Y0
);

  wire and_1_out, and_2_out, and_3_out, and_4_out, and_5_out, and_6_out, CLK_out, or_1_out, or_2_out,
       xor_1_out, xor_2_out;

  Clock CLK (.out(CLK_out));
  and and_1 (and_1_out, Y1, ~Y0, UP);  // AND_Gate
  and and_2 (and_2_out, ~Y1, ~Y0, ~UP);  // AND_Gate
  and and_3 (and_3_out, Y2, Y0);
  and and_4 (and_4_out, ~Y2, Y0, UP);  // AND_Gate
  and and_5 (and_5_out, Y2, Y0, ~UP);  // AND_Gate
  and and_6 (and_6_out, Y1, ~Y0);  // AND_Gate
  xor xor_1 (xor_1_out, Y2, Y1);
  D_Flip_Flop d_ff_1 (.D(or_1_out), .clk(CLK_out), .Q(Y2), .reset(RESET));  // open: Qn, preset
  or or_1 (or_1_out, and_1_out, and_2_out, and_3_out);
  D_Flip_Flop d_ff_2 (.D(or_2_out), .clk(CLK_out), .Q(Y1), .reset(RESET));  // open: Qn, preset
  or or_2 (or_2_out, and_4_out, and_5_out, and_6_out);
  D_Flip_Flop d_ff_3 (.D(xor_2_out), .clk(CLK_out), .Q(Y0), .reset(RESET));  // open: Qn, preset
  xor xor_2 (xor_2_out, UP, xor_1_out);
endmodule

module Exercise_329 (
  input  A,
  input  B,
  input  RESET,
  output Z
);

  wire and_1_out, and_2_out, and_3_out, CLK_out, d_ff_1_q;

  Clock CLK (.out(CLK_out));
  D_Flip_Flop d_ff_1 (.D(A), .clk(CLK_out), .Q(d_ff_1_q), .reset(RESET));  // open: Qn, preset
  and and_1 (and_1_out, d_ff_1_q, A);
  and and_2 (and_2_out, d_ff_1_q, B);
  or or_1 (Z, and_1_out, and_2_out, and_3_out);
  and and_3 (and_3_out, ~d_ff_1_q, A, B);  // AND_Gate
endmodule

module Exercise_330 (
  input  A,
  input  RESET,
  output X,
  output Y
);

  wire and_1_out, and_2_out, and_3_out, and_4_out, and_5_out, and_6_out, CLK_out, d_ff_1_q, d_ff_2_q,
       d_ff_3_q, d_ff_4_q, or_1_out, or_2_out, or_3_out;

  Clock CLK (.out(CLK_out));
  and and_1 (and_1_out, A, d_ff_2_q);
  and and_2 (and_2_out, d_ff_1_q, d_ff_2_q);
  and and_3 (and_3_out, ~d_ff_2_q, A);  // AND_Gate
  and and_4 (and_4_out, d_ff_2_q, ~A);  // AND_Gate
  and and_5 (and_5_out, ~d_ff_3_q, d_ff_4_q);  // AND_Gate
  and and_6 (and_6_out, d_ff_3_q, ~A);  // AND_Gate
  D_Flip_Flop d_ff_1 (.D(or_1_out), .clk(CLK_out), .Q(d_ff_1_q), .reset(RESET));  // open: Qn, preset
  or or_1 (or_1_out, and_1_out, d_ff_1_q);
  D_Flip_Flop d_ff_2 (.D(or_2_out), .clk(CLK_out), .Q(d_ff_2_q), .reset(RESET));  // open: Qn, preset
  or or_2 (or_2_out, and_2_out, and_3_out, and_4_out);
  D_Flip_Flop d_ff_3 (.D(A), .clk(CLK_out), .Q(d_ff_3_q), .reset(RESET));  // open: Qn, preset
  D_Flip_Flop d_ff_4 (.D(or_3_out), .clk(CLK_out), .Q(d_ff_4_q), .preset(RESET));  // open: Qn, reset
  or or_3 (or_3_out, and_5_out, and_6_out);
  and and_7 (X, d_ff_1_q, d_ff_2_q);
  and and_8 (Y, d_ff_3_q, ~d_ff_4_q);  // AND_Gate
endmodule
