// Logisim project Flip_Flops.circ as structural Verilog: 4 circuits, main circuit Exercise_39
module Exercise_39 (
  output Q
);

  wire CLK_out, not_1_out;

  D_Flip_Flop d_ff_1 (.D(not_1_out), .clk(CLK_out), .Q(Q));  // open: Qn, preset, reset
  not not_1 (not_1_out, Q);
  Clock CLK (.out(CLK_out));
endmodule

module Exercise_310A (
  input  J,
  input  K,
  output Q
);

  wire and_1_out, and_2_out, CLK_out, d_ff_1_qn, or_1_out;

  Clock CLK (.out(CLK_out));
  and and_1 (and_1_out, d_ff_1_qn, J);
  or or_1 (or_1_out, and_1_out, and_2_out);
  and and_2 (and_2_out, ~K, Q);  // AND_Gate
  D_Flip_Flop d_ff_1 (.D(or_1_out), .clk(CLK_out), .Q(Q), .Qn(d_ff_1_qn));  // open: preset, reset
endmodule

module Exercise_310B (
  input  D,
  output Q
);

  wire CLK_out, not_1_out;

  Clock CLK (.out(CLK_out));
  J_K_Flip_Flop j_k_ff_1 (.J(D), .K(not_1_out), .clk(CLK_out), .Q(Q));  // open: Qn, preset, reset
  not not_1 (not_1_out, D);
endmodule

module Exercise_310C (
  input  T,
  output Q
);

  wire CLK_out;

  Clock CLK (.out(CLK_out));
  J_K_Flip_Flop j_k_ff_1 (.J(T), .K(T), .clk(CLK_out), .Q(Q));  // open: Qn, preset, reset
endmodule
