// Logisim project Sync_Design.circ as structural Verilog: 4 circuits, main circuit Exercise_312
module Exercise_312 (
  input  R,
  input  D,
  input  E,
  output Q,
  output NQ
);

  wire nand_1_out, nand_2_out, not_1_out;

  not not_1 (not_1_out, R);
  nand nand_1 (nand_1_out, D, E);
  nand nand_2 (nand_2_out, nand_1_out, E);
  nand nand_3 (Q, not_1_out, nand_1_out, NQ);
  nand nand_4 (NQ, Q, nand_2_out);
endmodule

module Exercise_313 (
  input  D,
  input  R,
  output Q,
  output NQ
);

  wire CLK_out, nand_1_out, nand_2_out, nand_3_out, nand_4_out, not_1_out;

  Clock CLK (.out(CLK_out));
  not not_1 (not_1_out, R);
  nand nand_1 (nand_1_out, nand_4_out, nand_2_out);
  nand nand_2 (nand_2_out, not_1_out, nand_1_out, CLK_out);
  nand nand_3 (nand_3_out, nand_2_out, CLK_out, nand_4_out);
  nand nand_4 (nand_4_out, nand_3_out, D, not_1_out);
  nand nand_5 (Q, nand_2_out, NQ);
  nand nand_6 (NQ, Q, nand_3_out, not_1_out);
endmodule

module Exercise_314 (
  input  S,
  input  D,
  output Q,
  output NQ
);

  wire CLK_out, nand_1_out, nand_2_out, nand_3_out, nand_4_out, not_1_out;

  Clock CLK (.out(CLK_out));
  not not_1 (not_1_out, S);
  nand nand_1 (nand_1_out, not_1_out, nand_4_out, nand_2_out);
  nand nand_2 (nand_2_out, CLK_out, nand_1_out);
  nand nand_3 (nand_3_out, nand_2_out, CLK_out, nand_4_out);
  nand nand_4 (nand_4_out, nand_3_out, D);
  nand nand_5 (Q, nand_2_out, NQ);
  nand nand_6 (NQ, Q, nand_3_out);
endmodule

module Exercise_315 (
  input  S,
  input  D,
  output Q,
  output NQ
);

  wire CLK_out, nand_1_out, nand_2_out, nand_3_out, nand_4_out, not_1_out;

  Clock CLK (.out(CLK_out));
  not not_1 (not_1_out, S);
  nand nand_1 (nand_1_out, nand_4_out, nand_2_out);
  nand nand_2 (nand_2_out, nand_1_out, CLK_out);
  nand nand_3 (nand_3_out, nand_2_out, CLK_out, nand_4_out);
  nand nand_4 (nand_4_out, nand_3_out, D);
  nand nand_5 (Q, nand_2_out, not_1_out, NQ);
  nand nand_6 (NQ, Q, nand_3_out);
endmodule
