// Logisim project Priority_Log.circ as structural Verilog: 1 circuit, main circuit main
module main (
  input  A0,
  input  A1,
  input  A2,
  input  A3,
  input  A4,
  input  A5,
  input  A6,
  input  A7,
  output Y0,
  output Y1,
  output Y2
);

  wire and_2_out, and_3_out, and_4_out, and_6_out, and_7_out, and_8_out, and_9_out, and_10_out, and_11_out,
       and_12_out, and_13_out, and_14_out, and_15_out, and_16_out, and_17_out, and_18_out, and_19_out,
       not_1_out, not_2_out, not_3_out, not_4_out, not_5_out, not_6_out, not_7_out, not_8_out;

  not not_1 (not_1_out, A0);
  // AND_Gate and_1 has open pins: in0=A0, in1=and_8_out, out=open
  not not_2 (not_2_out, A2);
  not not_3 (not_3_out, A1);
  and and_2 (and_2_out, not_1_out, not_3_out);
  and and_3 (and_3_out, not_3_out, and_7_out);
  and and_4 (and_4_out, and_2_out, and_7_out);
  // AND_Gate and_5 has open pins: in0=and_4_out, in1=and_15_out, out=open
  and and_6 (and_6_out, A1, and_9_out);
  or or_1 (Y0, and_6_out, and_12_out, and_17_out, A7);
  not not_4 (not_4_out, A3);
  and and_7 (and_7_out, not_2_out, not_4_out);
  and and_8 (and_8_out, and_3_out, and_15_out);
  and and_9 (and_9_out, and_7_out, and_15_out);
  and and_10 (and_10_out, A2, and_11_out);
  not not_5 (not_5_out, A4);
  and and_11 (and_11_out, not_4_out, and_15_out);
  and and_12 (and_12_out, A3, and_15_out);
  and and_13 (and_13_out, A4, and_16_out);
  or or_2 (Y1, and_10_out, and_12_out, and_19_out, A7);
  not not_6 (not_6_out, A5);
  not not_7 (not_7_out, A6);
  and and_14 (and_14_out, not_5_out, not_6_out);
  and and_15 (and_15_out, and_14_out, and_18_out);
  and and_16 (and_16_out, not_6_out, and_18_out);
  and and_17 (and_17_out, A5, and_18_out);
  or or_3 (Y2, and_13_out, and_17_out, and_19_out, A7);
  not not_8 (not_8_out, A7);
  and and_18 (and_18_out, not_7_out, not_8_out);
  and and_19 (and_19_out, A6, not_8_out);
endmodule
