// Logisim project Signed_Comparator_4_bits.circ as structural Verilog: 1 circuit, main circuit main
module main (
  input  [3:0] A,
  input  [3:0] B,
  output [3:0] SUB,
  output LT
);

  wire xnor_1_out;
  wire [3:0] not_1_out;

  assign not_1_out = ~B;  // NOT_Gate not_1, 4 bits wide
  Adder #(.width(4)) adder_1 (.a(A), .b(not_1_out), .out(SUB), .cin(1'b1));  // open: cout
  xnor xnor_1 (xnor_1_out, A[3], B[3]);
  and and_1 (LT, SUB[3], xnor_1_out);
endmodule
