// Logisim project Unsigned_Comparator.circ as structural Verilog: 1 circuit, main circuit main
module main (
  input  N,
  input  Z,
  input  C,
  input  V,
  output LO,
  output LS,
  output HI,
  output HS
);

  not not_1 (LO, C);
  or or_1 (LS, Z, ~C);  // OR_Gate
  and and_1 (HI, ~Z, C);  // AND_Gate

  assign HS = C;
endmodule
