// Logisim project Signed_Comparator.circ as structural Verilog: 1 circuit, main circuit main
module main (
  input  N,
  input  Z,
  input  C,
  input  V,
  output LO,
  output LS,
  output HI,
  output HS
);

  xor xor_1 (LO, N, V);
  or or_1 (LS, LO, Z);
  and and_1 (HI, ~LO, ~Z);  // AND_Gate
  not not_1 (HS, LO);
endmodule
