// Logisim project rotate_shifters.circ as structural Verilog: 2 circuits, main circuit RR_shifter
module RR_shifter (
  input  [3:0] A,
  input  [1:0] SHAMT,
  output [3:0] Y
);

  Multiplexer #(.select(2)) multiplexer_1 (.in0(A[0]), .in1(A[1]), .in2(A[2]), .in3(A[3]), .out(Y[0]), .sel(SHAMT));
  Multiplexer #(.select(2)) multiplexer_2 (.in0(A[1]), .in1(A[2]), .in2(A[3]), .in3(A[0]), .out(Y[1]), .sel(SHAMT));
  Multiplexer #(.select(2)) multiplexer_3 (.in0(A[2]), .in1(A[3]), .in2(A[0]), .in3(A[1]), .out(Y[2]), .sel(SHAMT));
  Multiplexer #(.select(2)) multiplexer_4 (.in0(A[3]), .in1(A[0]), .in2(A[1]), .in3(A[2]), .out(Y[3]), .sel(SHAMT));
endmodule

module RL_shifter (
  input  [3:0] A,
  input  [1:0] SHAMT,
  output [3:0] Y
);

  Multiplexer #(.select(2)) multiplexer_1 (.in0(A[0]), .in1(A[3]), .in2(A[2]), .in3(A[1]), .out(Y[0]), .sel(SHAMT));
  Multiplexer #(.select(2)) multiplexer_2 (.in0(A[1]), .in1(A[0]), .in2(A[3]), .in3(A[2]), .out(Y[1]), .sel(SHAMT));
  Multiplexer #(.select(2)) multiplexer_3 (.in0(A[2]), .in1(A[1]), .in2(A[0]), .in3(A[3]), .out(Y[2]), .sel(SHAMT));
  Multiplexer #(.select(2)) multiplexer_4 (.in0(A[3]), .in1(A[2]), .in2(A[1]), .in3(A[0]), .out(Y[3]), .sel(SHAMT));
endmodule
