// Logisim project Left_Shifter_Mux_Array.circ as structural Verilog: 1 circuit, main circuit main
module main (
  input  [7:0] A,
  input  [2:0] SHAMT,
  output [7:0] Y
);

  wire multiplexer_1_out, multiplexer_2_out, multiplexer_4_out, multiplexer_5_out, multiplexer_6_out,
       multiplexer_8_out, multiplexer_9_out, multiplexer_10_out, multiplexer_13_out, multiplexer_14_out,
       multiplexer_16_out, multiplexer_17_out, multiplexer_18_out, multiplexer_20_out, multiplexer_21_out,
       multiplexer_22_out;

  Multiplexer multiplexer_1 (.in0(A[7]), .in1(A[6]), .out(multiplexer_1_out));  // open: sel
  Multiplexer multiplexer_2 (.in0(multiplexer_1_out), .in1(multiplexer_5_out), .out(multiplexer_2_out));  // open: sel
  Multiplexer multiplexer_3 (.in0(multiplexer_2_out), .in1(multiplexer_14_out), .out(Y[7]));  // open: sel
  Multiplexer multiplexer_4 (.in0(A[6]), .in1(A[5]), .out(multiplexer_4_out));  // open: sel
  Multiplexer multiplexer_5 (.in0(A[5]), .in1(A[4]), .out(multiplexer_5_out));  // open: sel
  Multiplexer multiplexer_6 (.in0(multiplexer_4_out), .in1(multiplexer_8_out), .out(multiplexer_6_out));  // open: sel
  Multiplexer multiplexer_7 (.in0(multiplexer_6_out), .in1(multiplexer_18_out), .out(Y[6]));  // open: sel
  Multiplexer multiplexer_8 (.in0(A[4]), .in1(A[3]), .out(multiplexer_8_out));  // open: sel
  Multiplexer multiplexer_9 (.in0(multiplexer_5_out), .in1(multiplexer_13_out), .out(multiplexer_9_out));  // open: sel
  Multiplexer multiplexer_10 (
    .in0(multiplexer_8_out), .in1(multiplexer_16_out), .out(multiplexer_10_out));  // open: sel
  Multiplexer multiplexer_11 (.in0(multiplexer_9_out), .in1(multiplexer_21_out), .out(Y[5]));  // open: sel
  Multiplexer multiplexer_12 (.in0(multiplexer_10_out), .in1(multiplexer_22_out), .out(Y[4]));  // open: sel
  Multiplexer multiplexer_13 (.in0(A[3]), .in1(A[2]), .out(multiplexer_13_out));  // open: sel
  Multiplexer multiplexer_14 (
    .in0(multiplexer_13_out), .in1(multiplexer_17_out), .out(multiplexer_14_out));  // open: sel
  Multiplexer multiplexer_15 (.in0(multiplexer_14_out), .in1(1'b0), .out(Y[3]));  // open: sel
  Multiplexer multiplexer_16 (.in0(A[2]), .in1(A[1]), .out(multiplexer_16_out));  // open: sel
  Multiplexer multiplexer_17 (.in0(A[1]), .in1(A[0]), .out(multiplexer_17_out));  // open: sel
  Multiplexer multiplexer_18 (
    .in0(multiplexer_16_out), .in1(multiplexer_20_out), .out(multiplexer_18_out));  // open: sel
  Multiplexer multiplexer_19 (.in0(multiplexer_18_out), .in1(1'b0), .out(Y[2]));  // open: sel
  Multiplexer multiplexer_20 (.in0(A[0]), .in1(1'b0), .out(multiplexer_20_out));  // open: sel
  Multiplexer multiplexer_21 (.in0(multiplexer_17_out), .in1(1'b0), .out(multiplexer_21_out));  // open: sel
  Multiplexer multiplexer_22 (.in0(multiplexer_20_out), .in1(1'b0), .out(multiplexer_22_out));  // open: sel
  Multiplexer multiplexer_23 (.in0(multiplexer_21_out), .in1(1'b0), .out(Y[1]));  // open: sel
  Multiplexer multiplexer_24 (.in0(multiplexer_22_out), .in1(1'b0), .out(Y[0]));  // open: sel
endmodule
