// Logisim project Signed_Multiplicator.circ as structural Verilog: 1 circuit, main circuit main
module main (
  input  [3:0] A,
  input  [3:0] B,
  output [7:0] Y
);

  wire xor_1_out;
  wire [3:0] multiplexer_1_out, multiplexer_2_out, multiplier_1_cout, multiplier_1_out, negator_1_out,
       negator_2_out;
  wire [7:0] negator_3_out;

  Multiplexer #(.width(4)) multiplexer_1 (.in0(A), .in1(negator_1_out), .out(multiplexer_1_out), .sel(A[3]));
  Negator #(.width(4)) negator_1 (.in(A), .out(negator_1_out));
  Multiplexer #(.width(4)) multiplexer_2 (.in0(B), .in1(negator_2_out), .out(multiplexer_2_out), .sel(B[3]));
  Negator #(.width(4)) negator_2 (.in(B), .out(negator_2_out));
  Multiplier #(.width(4)) multiplier_1 (
    .a(multiplexer_1_out), .b(multiplexer_2_out), .out(multiplier_1_out), .cout(multiplier_1_cout));  // open: cin
  xor xor_1 (xor_1_out, A[3], B[3]);
  Negator negator_3 (.in({multiplier_1_cout, multiplier_1_out}), .out(negator_3_out));
  Multiplexer #(.width(8)) multiplexer_3 (
    .in0({multiplier_1_cout, multiplier_1_out}), .in1(negator_3_out), .out(Y), .sel(xor_1_out));
endmodule
