// Logisim project Extensions.circ as structural Verilog: 2 circuits, main circuit Sign_Extended
module Sign_Extended (
  input  [3:0] A,
  output [7:0] Y
);


  assign Y = {{5{A[3]}}, A[2:0]};
endmodule

module Zero_Extended (
  input  [3:0] A,
  output [7:0] Y
);


  assign Y = {4'b0000, A};
endmodule
