// Logisim project Counter_Half_Add.circ as structural Verilog: 1 circuit, main circuit main
module main (
  input  RESET,
  output [7:0] Y
);

  wire adder_1_cout, adder_1_out, adder_2_cout, adder_2_out, adder_3_cout, adder_3_out, adder_4_cout,
       adder_4_out, adder_5_cout, adder_5_out, adder_6_cout, adder_6_out, adder_7_cout, adder_7_out,
       adder_8_out, CLK_out;

  D_Flip_Flop d_ff_1 (.D(adder_1_out), .clk(CLK_out), .Q(Y[0]), .reset(RESET));  // open: Qn, preset
  Adder #(.width(1)) adder_1 (.a(1'b1), .b(Y[0]), .out(adder_1_out), .cout(adder_1_cout));  // open: cin
  D_Flip_Flop d_ff_2 (.D(adder_2_out), .clk(CLK_out), .Q(Y[1]), .reset(RESET));  // open: Qn, preset
  Adder #(.width(1)) adder_2 (.a(adder_1_cout), .b(Y[1]), .out(adder_2_out), .cout(adder_2_cout));  // open: cin
  D_Flip_Flop d_ff_3 (.D(adder_3_out), .clk(CLK_out), .Q(Y[2]), .reset(RESET));  // open: Qn, preset
  Adder #(.width(1)) adder_3 (.a(adder_2_cout), .b(Y[2]), .out(adder_3_out), .cout(adder_3_cout));  // open: cin
  D_Flip_Flop d_ff_4 (.D(adder_4_out), .clk(CLK_out), .Q(Y[3]), .reset(RESET));  // open: Qn, preset
  Adder #(.width(1)) adder_4 (.a(adder_3_cout), .b(Y[3]), .out(adder_4_out), .cout(adder_4_cout));  // open: cin
  D_Flip_Flop d_ff_5 (.D(adder_5_out), .clk(CLK_out), .Q(Y[4]), .reset(RESET));  // open: Qn, preset
  Adder #(.width(1)) adder_5 (.a(adder_4_cout), .b(Y[4]), .out(adder_5_out), .cout(adder_5_cout));  // open: cin
  D_Flip_Flop d_ff_6 (.D(adder_6_out), .clk(CLK_out), .Q(Y[5]), .reset(RESET));  // open: Qn, preset
  Adder #(.width(1)) adder_6 (.a(adder_5_cout), .b(Y[5]), .out(adder_6_out), .cout(adder_6_cout));  // open: cin
  D_Flip_Flop d_ff_7 (.D(adder_7_out), .clk(CLK_out), .Q(Y[6]), .reset(RESET));  // open: Qn, preset
  Adder #(.width(1)) adder_7 (.a(adder_6_cout), .b(Y[6]), .out(adder_7_out), .cout(adder_7_cout));  // open: cin
  D_Flip_Flop d_ff_8 (.D(adder_8_out), .clk(CLK_out), .Q(Y[7]), .reset(RESET));  // open: Qn, preset
  Adder #(.width(1)) adder_8 (.a(adder_7_cout), .b(Y[7]), .out(adder_8_out));  // open: cin, cout
  Clock CLK (.out(CLK_out));
endmodule
