// Logisim project Up_Down_Counter.circ as structural Verilog: 1 circuit, main circuit main
module main (
  input  UP,
  input  RESET,
  output [31:0] Y
);

  wire CLK_out, not_2_out;
  wire [31:0] adder_1_out, multiplexer_1_out, not_1_out;

  assign not_1_out = ~32'h1;  // NOT_Gate not_1, 32 bits wide
  not not_2 (not_2_out, UP);
  Multiplexer #(.width(32)) multiplexer_1 (.in0(not_1_out), .in1(32'h1), .out(multiplexer_1_out));  // open: sel
  Clock CLK (.out(CLK_out));
  Register #(.width(32)) register_1 (.D(adder_1_out), .clk(CLK_out), .Q(Y), .clr(RESET));  // open: en
  Adder #(.width(32)) adder_1 (.a(multiplexer_1_out), .b(Y), .out(adder_1_out), .cin(not_2_out));  // open: cout
endmodule
