// Logisim project Counter_Four.circ as structural Verilog: 1 circuit, main circuit main
module main (
  input  RESET
);

  wire CLK_out;
  wire [31:0] adder_1_out, register_1_q;

  Adder #(.width(32)) adder_1 (.a(register_1_q), .b(32'h4), .out(adder_1_out));  // open: cin, cout
  Clock CLK (.out(CLK_out));
  Register #(.width(32)) register_1 (.D(adder_1_out), .clk(CLK_out), .Q(register_1_q), .clr(RESET));  // open: en
endmodule
