// Logisim project Counter_Load.circ as structural Verilog: 1 circuit, main circuit main
module main (
  input  [31:0] D,
  input  RESET,
  input  LOAD
);

  wire CLK_out;
  wire [31:0] adder_1_out, multiplexer_1_out, register_1_q;

  Adder #(.width(32)) adder_1 (.a(register_1_q), .b(32'h4), .out(adder_1_out));  // open: cin, cout
  Register #(.width(32)) register_1 (.D(multiplexer_1_out), .clk(CLK_out), .Q(register_1_q), .clr(RESET));  // open: en
  Multiplexer #(.width(32)) multiplexer_1 (.in0(adder_1_out), .in1(D), .out(multiplexer_1_out), .sel(LOAD));
  Clock CLK (.out(CLK_out));
endmodule
