// Logisim project Johnson_Counter.circ as structural Verilog: 1 circuit, main circuit main
module main (
  input  RST,
  output [9:0] SEQ_DEC
);

  wire CLK_out, d_ff_1_q, d_ff_2_q, d_ff_3_q, d_ff_4_q, d_ff_5_q, d_ff_5_qn;

  and and_1 (SEQ_DEC[0], ~d_ff_5_q, ~d_ff_1_q);  // AND_Gate
  and and_2 (SEQ_DEC[1], d_ff_1_q, ~d_ff_2_q);  // AND_Gate
  D_Flip_Flop d_ff_1 (.D(d_ff_5_qn), .clk(CLK_out), .Q(d_ff_1_q), .reset(RST));  // open: Qn, preset
  Clock CLK (.out(CLK_out));
  and and_3 (SEQ_DEC[2], d_ff_2_q, ~d_ff_3_q);  // AND_Gate
  and and_4 (SEQ_DEC[3], d_ff_3_q, ~d_ff_4_q);  // AND_Gate
  D_Flip_Flop d_ff_2 (.D(d_ff_1_q), .clk(CLK_out), .Q(d_ff_2_q), .reset(RST));  // open: Qn, preset
  and and_5 (SEQ_DEC[4], d_ff_4_q, ~d_ff_5_q);  // AND_Gate
  and and_6 (SEQ_DEC[5], d_ff_5_q, d_ff_1_q);
  D_Flip_Flop d_ff_3 (.D(d_ff_2_q), .clk(CLK_out), .Q(d_ff_3_q), .reset(RST));  // open: Qn, preset
  and and_7 (SEQ_DEC[6], ~d_ff_1_q, d_ff_2_q);  // AND_Gate
  and and_8 (SEQ_DEC[7], ~d_ff_2_q, d_ff_3_q);  // AND_Gate
  D_Flip_Flop d_ff_4 (.D(d_ff_3_q), .clk(CLK_out), .Q(d_ff_4_q), .reset(RST));  // open: Qn, preset
  and and_9 (SEQ_DEC[8], ~d_ff_3_q, d_ff_4_q);  // AND_Gate
  and and_10 (SEQ_DEC[9], ~d_ff_4_q, d_ff_5_q);  // AND_Gate
  D_Flip_Flop d_ff_5 (.D(d_ff_4_q), .clk(CLK_out), .Q(d_ff_5_q), .Qn(d_ff_5_qn), .reset(RST));  // open: preset
endmodule
