// Logisim project Encode_2bit_miss.circ as structural Verilog: 1 circuit, main circuit main
module main (
  input  A4,
  input  A3,
  input  A2,
  input  A1,
  input  A0,
  output [1:0] Y
);

  wire and_1_out, and_2_out, and_3_out, and_4_out, and_5_out, and_6_out, and_7_out, and_8_out, and_9_out,
       and_10_out, and_11_out, and_12_out, and_13_out, and_14_out, and_15_out, and_18_out, and_19_out,
       and_20_out, and_21_out, and_22_out, or_1_out, or_2_out, or_3_out, or_4_out;
  wire [19:0] xnor_20_out;

  xnor xnor_1 (xnor_20_out[18], 1'b1, A4);
  xnor xnor_2 (xnor_20_out[19], 1'b1, A4);
  xnor xnor_3 (xnor_20_out[17], 1'b0, A4);
  xnor xnor_4 (xnor_20_out[16], 1'b0, A4);
  and and_1 (and_1_out, xnor_20_out[3], xnor_20_out[7], xnor_20_out[11], xnor_20_out[15]);
  and and_2 (and_2_out, xnor_20_out[7], xnor_20_out[11], xnor_20_out[15], xnor_20_out[19]);
  and and_3 (and_3_out, xnor_20_out[3], xnor_20_out[11], xnor_20_out[15], xnor_20_out[19]);
  and and_4 (and_4_out, xnor_20_out[3], xnor_20_out[7], xnor_20_out[15], xnor_20_out[19]);
  and and_5 (and_5_out, xnor_20_out[3], xnor_20_out[7], xnor_20_out[11], xnor_20_out[19]);
  xnor xnor_5 (xnor_20_out[15], 1'b0, A3);
  xnor xnor_6 (xnor_20_out[14], 1'b1, A3);
  or or_1 (or_1_out, and_1_out, and_2_out, and_3_out, and_4_out, and_5_out);
  xnor xnor_7 (xnor_20_out[13], 1'b0, A3);
  xnor xnor_8 (xnor_20_out[12], 1'b1, A3);
  and and_6 (and_6_out, xnor_20_out[2], xnor_20_out[6], xnor_20_out[10], xnor_20_out[14]);
  and and_7 (and_7_out, xnor_20_out[6], xnor_20_out[10], xnor_20_out[14], xnor_20_out[18]);
  and and_8 (and_8_out, xnor_20_out[2], xnor_20_out[10], xnor_20_out[14], xnor_20_out[18]);
  and and_9 (and_9_out, xnor_20_out[2], xnor_20_out[6], xnor_20_out[14], xnor_20_out[18]);
  and and_10 (and_10_out, xnor_20_out[2], xnor_20_out[6], xnor_20_out[10], xnor_20_out[18]);
  xnor xnor_9 (xnor_20_out[11], 1'b0, A2);
  xnor xnor_10 (xnor_20_out[10], 1'b0, A2);
  or or_2 (or_2_out, and_6_out, and_7_out, and_8_out, and_9_out, and_10_out);
  xnor xnor_11 (xnor_20_out[9], 1'b1, A2);
  xnor xnor_12 (xnor_20_out[8], 1'b1, A2);
  and and_11 (and_11_out, xnor_20_out[1], xnor_20_out[5], xnor_20_out[9], xnor_20_out[13]);
  and and_12 (and_12_out, xnor_20_out[5], xnor_20_out[9], xnor_20_out[13], xnor_20_out[17]);
  and and_13 (and_13_out, xnor_20_out[1], xnor_20_out[9], xnor_20_out[13], xnor_20_out[17]);
  and and_14 (and_14_out, xnor_20_out[1], xnor_20_out[5], xnor_20_out[13], xnor_20_out[17]);
  and and_15 (and_15_out, xnor_20_out[1], xnor_20_out[5], xnor_20_out[9], xnor_20_out[17]);
  xnor xnor_13 (xnor_20_out[7], 1'b0, A1);
  xnor xnor_14 (xnor_20_out[6], 1'b1, A1);
  or or_3 (or_3_out, and_11_out, and_12_out, and_13_out, and_14_out, and_15_out);
  and and_16 (Y[1], or_2_out, or_3_out);
  and and_17 (Y[0], or_3_out, or_4_out);
  xnor xnor_15 (xnor_20_out[5], 1'b0, A1);
  xnor xnor_16 (xnor_20_out[4], 1'b1, A1);
  xnor xnor_17 (xnor_20_out[3], 1'b1, A0);
  xnor xnor_18 (xnor_20_out[2], 1'b0, A0);
  and and_18 (and_18_out, xnor_20_out[0], xnor_20_out[4], xnor_20_out[8], xnor_20_out[12]);
  and and_19 (and_19_out, xnor_20_out[4], xnor_20_out[8], xnor_20_out[12], xnor_20_out[16]);
  and and_20 (and_20_out, xnor_20_out[0], xnor_20_out[8], xnor_20_out[12], xnor_20_out[16]);
  or or_4 (or_4_out, and_18_out, and_19_out, and_20_out, and_21_out, and_22_out);
  and and_21 (and_21_out, xnor_20_out[0], xnor_20_out[4], xnor_20_out[12], xnor_20_out[16]);
  and and_22 (and_22_out, xnor_20_out[0], xnor_20_out[4], xnor_20_out[8], xnor_20_out[16]);
  xnor xnor_19 (xnor_20_out[1], 1'b0, A0);
  xnor xnor_20 (xnor_20_out[0], 1'b1, A0);
endmodule
